// Logisim project 4_bit_ALU.circ as structural Verilog: 1 circuit, main circuit main
module main (
  input  Cin,
  input  [3:0] S3S2S1S0,
  input  [3:0] A3A2A1A0,
  input  [3:0] B3B2B1B0,
  output [3:0] D0D1D2D3,
  output Cout,
  output [3:0] out_7
);

  wire main_5_p6, main_6_p6, main_7_p6;
  wire [3:0] main_5_p5, multiplexer_1_out, multiplexer_2_out;

  // _1bit_logic_circuit_main main_1: pin names not known; wires that end beside it: A3A2A1A0[0], B3B2B1B0[0], S3S2S1S0[1:0], out_7[0]
  // _1bit_logic_circuit_main main_2: pin names not known; wires that end beside it: A3A2A1A0[1], B3B2B1B0[1], S3S2S1S0[1:0], out_7[1]
  // _1bit_logic_circuit_main main_3: pin names not known; wires that end beside it: A3A2A1A0[2], B3B2B1B0[2], S3S2S1S0[1:0], out_7[2]
  // _1bit_logic_circuit_main main_4: pin names not known; wires that end beside it: A3A2A1A0[3], B3B2B1B0[3], S3S2S1S0[1:0], out_7[3]
  // Arithmetic_circuit_1_bit_main main_5: pin names not known; wires that end beside it: Cin, B3B2B1B0[0], A3A2A1A0[0], S3S2S1S0[1:0], main_5_p5[0], main_5_p6
  // Arithmetic_circuit_1_bit_main main_6: pin names not known; wires that end beside it: main_5_p6, B3B2B1B0[1], A3A2A1A0[1], S3S2S1S0[1:0], main_5_p5[1], main_6_p6
  // Arithmetic_circuit_1_bit_main main_7: pin names not known; wires that end beside it: main_6_p6, B3B2B1B0[2], A3A2A1A0[2], S3S2S1S0[1:0], main_5_p5[2], main_7_p6
  // Arithmetic_circuit_1_bit_main main_8: pin names not known; wires that end beside it: main_7_p6, B3B2B1B0[3], A3A2A1A0[3], S3S2S1S0[1:0], main_5_p5[3], Cout
  Multiplexer #(.select(2), .width(4), .enable("false")) multiplexer_1 (
    .in0({A3A2A1A0[2:0], 1'b0}), .in1({A3A2A1A0[2:0], 1'b0}), .in2({A3A2A1A0[2:0], A3A2A1A0[3]}),
    .out(multiplexer_1_out), .sel(S3S2S1S0[1:0]));  // open: in3
  Multiplexer #(.select(2), .width(4), .enable("false")) multiplexer_2 (
    .in0({{2{A3A2A1A0[3]}}, A3A2A1A0[2:1]}), .in1({A3A2A1A0[0], A3A2A1A0[3:1]}), .in3({1'b0, A3A2A1A0[3:1]}),
    .out(multiplexer_2_out), .sel(S3S2S1S0[1:0]));  // open: in2
  Multiplexer #(.select(2), .width(4), .enable("false")) multiplexer_3 (
    .in0(main_5_p5), .in1(out_7), .in2(multiplexer_1_out), .in3(multiplexer_2_out), .out(D0D1D2D3),
    .sel(S3S2S1S0[3:2]));

  // Other names for the same wires on the sheet: A0 = A3A2A1A0[0]; A1 = A3A2A1A0[1]; A2 = A3A2A1A0[2];
  //   A3 = A3A2A1A0[3]; B0 = B3B2B1B0[0]; B1 = B3B2B1B0[1]; B2 = B3B2B1B0[2]; B3 = B3B2B1B0[3];
  //   S1S0[1:0] = S3S2S1S0[1:0]; S3S2[1:0] = S3S2S1S0[3:2]

  // Notes on the sheet:
  //   A3A2A1A0
endmodule
