// Logisim project Basic_Computer.circ as structural Verilog: 6 circuits, main circuit main
module main (
);

  wire AC_CLR, AC_INC, AC_LD, alu1bit_1_cout, alu1bit_2_cout, alu1bit_3_cout, alu1bit_4_cout, alu1bit_5_cout,
       alu1bit_6_cout, alu1bit_7_cout, alu1bit_8_cout, alu1bit_9_cout, alu1bit_10_cout, alu1bit_11_cout,
       alu1bit_12_cout, alu1bit_13_cout, alu1bit_14_cout, alu1bit_15_cout, alu1bit_16_cout, ALU_CIN,
       and_3_out, and_4_out, and_5_out, and_7_out, and_8_out, and_9_out, and_10_out, and_11_out, and_12_out,
       and_13_out, and_14_out, and_15_out, and_16_out, and_17_out, and_18_out, and_19_out, and_20_out,
       and_21_out, and_22_out, and_23_out, and_24_out, and_25_out, and_30_out, and_31_out, and_32_out,
       and_33_out, and_34_out, and_35_out, and_36_out, and_37_out, and_38_out, and_39_out, and_40_out,
       and_41_out, and_42_out, and_43_out, and_44_out, and_45_out, and_46_out, and_47_out, and_48_out,
       and_49_out, and_54_out, and_55_out, and_56_out, and_57_out, and_58_out, and_59_out, AR_CLR, AR_INC,
       AR_LD, B0, B1, B2, B3, B4, B5, B6, B7, B8, B9, B10, B11, CLOCK, comparator_1_eq, comparator_2_eq, D0,
       D1, D2, D3, D4, D5, D6, D7, DR_INC, DR_LD, E, E_LD, EIN, FGI, FGO, I, IEN_q, IR_LD, not_1_out,
       not_2_out, not_3_out, not_4_out, not_5_out, not_6_out, not_7_out, not_8_out, not_9_out, or_9_out,
       or_10_out, or_11_out, OUTR_LD, p, PC_CLR, PC_INC, PC_LD, R, R_prime, r_t, RAM_LD, SC_CLR, T0, T1, T2,
       T3, T4, T5, T6, T7, T8, T9, T10, T11, T12, T13, T14, T15, TR_LD;
  wire [1:0] E_SELECT;
  wire [2:0] BUS;
  wire [3:0] ALU_SELECT, multiplexer_1_out_2, SC_q;
  wire [11:0] AR, multiplexer_1_out, PC_q;
  wire [15:0] AC, AC_IN, ALU_X, ALU_Y, DR, ram_1_data, TR_q;
  wire [15:12] IR;

  Comparator #(.width(16)) comparator_1 (.a(DR), .b({16{1'b0}}), .eq(comparator_1_eq));  // open: gt, lt
  Comparator #(.width(16)) comparator_2 (.a(AC), .b({16{1'b0}}), .eq(comparator_2_eq));  // open: gt, lt
  REG12BIT u_AR (.D(multiplexer_1_out), .INC(AR_INC), .CLK(CLOCK), .CLR(AR_CLR), .Q(AR), .LD(AR_LD));
  REG12BIT PC (.D(multiplexer_1_out), .INC(PC_INC), .CLK(CLOCK), .CLR(PC_CLR), .Q(PC_q), .LD(PC_LD));
  REG16BIT u_AC (.INC(AC_INC), .CLK(CLOCK), .CLR(AC_CLR), .Q(AC), .LD(AC_LD));  // open: D
  REG16BIT u_DR (
    .D({multiplexer_1_out_2, multiplexer_1_out}), .INC(DR_INC), .CLK(CLOCK), .Q(DR), .LD(DR_LD));  // open: CLR
  REG16BIT u_IR (
    .D({multiplexer_1_out_2, multiplexer_1_out}), .CLK(CLOCK),
    .Q({IR, B11, B10, B9, B8, B7, B6, B5, B4, B3, B2, B1, B0}), .LD(IR_LD));  // open: INC, CLR
  REG16BIT TR (.D({multiplexer_1_out_2, multiplexer_1_out}), .CLK(CLOCK), .Q(TR_q));  // open: INC, CLR, LD
  REG8BIT OUTR (.D(multiplexer_1_out[7:0]), .CLK(CLOCK), .LD(OUTR_LD));  // open: INC, CLR, Q
  not not_1 (not_1_out, D7);
  not not_2 (not_2_out, AC[15]);
  not not_3 (not_3_out, E);
  not not_4 (not_4_out, FGO);
  RAM #(.addrWidth(12), .dataWidth(16), .bus("separate")) ram_1 (
    .addr(AR), .din({multiplexer_1_out_2, multiplexer_1_out}), .data(ram_1_data), .clk(CLOCK), .ld(RAM_LD));  // open: str, sel, clr
  and and_1 (AR_CLR, R, T0);
  and and_2 (AR_INC, D5, T4);
  and and_3 (and_3_out, R_prime, T2);
  and and_4 (and_4_out, not_1_out, I, T3);
  and and_5 (and_5_out, R_prime, T0);
  and and_6 (PC_CLR, R, T1);
  and and_7 (and_7_out, D4, T4);
  and and_8 (and_8_out, D5, T5);
  and and_9 (and_9_out, R_prime, T1);
  and and_10 (and_10_out, R, T2);
  and and_11 (and_11_out, r_t, AC[15], B3);
  and and_12 (and_12_out, D6, comparator_1_eq, T6);
  and and_13 (and_13_out, r_t, not_2_out, B4);
  and and_14 (and_14_out, r_t, comparator_2_eq, B4);
  and and_15 (and_15_out, r_t, not_3_out, B4);
  and and_16 (and_16_out, p, FGI, B9);
  and and_17 (and_17_out, p, not_4_out, B8);
  or or_1 (AR_LD, and_3_out, and_4_out, and_5_out);
  or or_2 (PC_LD, and_7_out, and_8_out);
  Multiplexer #(.select(3), .width(16), .enable("false")) multiplexer_1 (
    .in1({4'b0000, AR}), .in2({4'b0000, PC_q}), .in5(AC), .in6(DR),
    .in7({IR, B11, B10, B9, B8, B7, B6, B5, B4, B3, B2, B1, B0}),
    .out({multiplexer_1_out_2, multiplexer_1_out}), .sel(BUS));  // open: in0, in3, in4
  or or_3 (PC_INC, and_9_out, and_10_out, and_11_out, and_12_out, and_13_out, and_14_out, and_15_out, and_16_out, and_17_out);
  REG8BIT INPR ();  // open: D, INC, CLK, CLR, Q, LD
  and and_18 (and_18_out, R, T1);
  and and_19 (and_19_out, D3, T4);
  and and_20 (and_20_out, D5, T4);
  and and_21 (and_21_out, D1, T5);
  and and_22 (and_22_out, r_t, B7);
  and and_23 (and_23_out, r_t, B6);
  and and_24 (and_24_out, r_t, B10);
  and and_25 (and_25_out, r_t, B8);
  and and_26 (TR_LD, R, T0);
  and and_27 (OUTR_LD, p, B10);
  and and_28 (IR_LD, R_prime, T1);
  and and_29 (DR_INC, D6, T5);
  and and_30 (and_30_out, D0, T4);
  and and_31 (and_31_out, D1, T4);
  and and_32 (and_32_out, D2, T4);
  and and_33 (and_33_out, D6, T4);
  or or_4 (DR_LD, and_30_out, and_31_out, and_32_out, and_33_out);
  Clock clock_1 (.out(CLOCK));
  or or_5 (E_LD, and_21_out, and_22_out, and_23_out, and_24_out, and_25_out);
  or or_6 (RAM_LD, and_18_out, and_19_out, and_20_out);
  D_Flip_Flop u_E (.D(EIN), .Q(E), .en(E_LD));  // open: clk, Qn, preset, reset
  Counter #(.width(4), .max('hf)) SC (.load(SC_CLR), .D(4'b0000), .Q(SC_q), .clk(CLOCK));  // open: count, carry, clr
  Decoder #(.select(4), .enable("false")) decoder_1 (
    .out0(T0), .out1(T1), .out2(T2), .out3(T3), .out4(T4), .out5(T5), .out6(T6), .out7(T7), .out8(T8),
    .out9(T9), .out10(T10), .out11(T11), .out12(T12), .out13(T13), .out14(T14), .out15(T15), .sel(SC_q));
  and and_34 (and_34_out, R, T2);
  and and_35 (and_35_out, D0, T5);
  and and_36 (and_36_out, D1, T5);
  and and_37 (and_37_out, D2, T5);
  and and_38 (and_38_out, D3, T4);
  and and_39 (and_39_out, D4, T4);
  and and_40 (and_40_out, D5, T5);
  and and_41 (and_41_out, D6, T6);
  not not_5 (not_5_out, I);
  and and_42 (and_42_out, R_prime, T2);
  and and_43 (and_43_out, D0, T5);
  and and_44 (and_44_out, D1, T5);
  and and_45 (and_45_out, D2, T5);
  and and_46 (and_46_out, r_t, B9);
  and and_47 (and_47_out, r_t, B7);
  and and_48 (and_48_out, r_t, B6);
  and and_49 (and_49_out, p, B11);
  and and_50 (AC_INC, r_t, B5);
  and and_51 (AC_CLR, r_t, B11);
  and and_52 (r_t, D7, not_5_out, T3);
  D_Flip_Flop u_I (.clk(CLOCK), .D(IR[15]), .Q(I), .en(and_42_out));  // open: Qn, preset, reset
  or or_7 (AC_LD, and_43_out, and_44_out, and_45_out, and_46_out, and_47_out, and_48_out, and_49_out);
  and and_53 (p, D7, I, T3);
  Decoder #(.select(3), .enable("false")) decoder_2 (
    .out0(D0), .out1(D1), .out2(D2), .out3(D3), .out4(D4), .out5(D5), .out6(D6), .out7(D7), .sel(IR[14:12]));
  or or_8 (SC_CLR, and_34_out, and_35_out, and_36_out, and_37_out, and_38_out, and_39_out, and_40_out, and_41_out, r_t, p);
  and and_54 (and_54_out, p, B11);
  and and_55 (and_55_out, p, B10);
  // Probe on ALU_X
  and and_56 (and_56_out, p, B7);
  and and_57 (and_57_out, p, B6);
  // Probe on ALU_Y
  or or_9 (or_9_out, and_56_out, and_57_out);
  D_Flip_Flop IEN (.clk(CLOCK), .D(or_9_out), .Q(IEN_q));  // open: Qn, preset, en, reset
  D_Flip_Flop u_FGI (.clk(CLOCK), .Q(FGI), .preset(and_54_out), .en(and_54_out));  // open: D, Qn, reset
  D_Flip_Flop u_FGO (.clk(CLOCK), .Q(FGO), .en(and_55_out));  // open: D, Qn, preset, reset
  not not_6 (not_6_out, T0);
  not not_7 (not_7_out, T2);
  Multiplexer #(.select(2), .enable("false")) multiplexer_2 (
    .in0(ALU_Y[0]), .in1(ALU_Y[15]), .in2(alu1bit_16_cout), .in3(alu1bit_16_cout), .out(EIN), .sel(E_SELECT));
  not not_8 (not_8_out, T1);
  or or_10 (or_10_out, FGI, FGO);
  and and_58 (and_58_out, IEN_q, not_6_out, not_8_out, not_7_out, or_10_out);
  or or_11 (or_11_out, and_59_out, and_58_out);
  ALU1Bit alu1bit_1 (
    .Cin(ALU_CIN), .Ai(ALU_Y[0]), .Bi(ALU_X[0]), .S3S2S1S0(ALU_SELECT), .Ai_1(E), .Ai_1_2(ALU_Y[1]),
    .out_7(AC_IN[0]), .Cout(alu1bit_1_cout));
  ALU1Bit alu1bit_2 (
    .Cin(alu1bit_1_cout), .Ai(ALU_Y[1]), .Bi(ALU_X[1]), .S3S2S1S0(ALU_SELECT), .Ai_1(ALU_Y[0]),
    .Ai_1_2(ALU_Y[1]), .out_7(AC_IN[1]), .Cout(alu1bit_2_cout));
  ALU1Bit alu1bit_3 (
    .Cin(alu1bit_2_cout), .Ai(ALU_Y[2]), .Bi(ALU_X[2]), .S3S2S1S0(ALU_SELECT), .Ai_1(ALU_Y[1]),
    .Ai_1_2(ALU_Y[2]), .out_7(AC_IN[2]), .Cout(alu1bit_3_cout));
  ALU1Bit alu1bit_4 (
    .Cin(alu1bit_3_cout), .Ai(ALU_Y[3]), .Bi(ALU_X[3]), .S3S2S1S0(ALU_SELECT), .Ai_1(ALU_Y[2]),
    .Ai_1_2(ALU_Y[3]), .out_7(AC_IN[3]), .Cout(alu1bit_4_cout));
  ALU1Bit alu1bit_5 (
    .Cin(alu1bit_4_cout), .Ai(ALU_Y[4]), .Bi(ALU_X[4]), .S3S2S1S0(ALU_SELECT), .Ai_1(ALU_Y[3]),
    .Ai_1_2(ALU_Y[4]), .out_7(AC_IN[4]), .Cout(alu1bit_5_cout));
  ALU1Bit alu1bit_6 (
    .Cin(alu1bit_5_cout), .Ai(ALU_Y[5]), .Bi(ALU_X[5]), .S3S2S1S0(ALU_SELECT), .Ai_1(ALU_Y[4]),
    .Ai_1_2(ALU_Y[5]), .out_7(AC_IN[5]), .Cout(alu1bit_6_cout));
  ALU1Bit alu1bit_7 (
    .Cin(alu1bit_6_cout), .Ai(ALU_Y[6]), .Bi(ALU_X[6]), .S3S2S1S0(ALU_SELECT), .Ai_1(ALU_Y[5]),
    .Ai_1_2(ALU_Y[6]), .out_7(AC_IN[6]), .Cout(alu1bit_7_cout));
  ALU1Bit alu1bit_8 (
    .Cin(alu1bit_7_cout), .Ai(ALU_Y[7]), .Bi(ALU_X[7]), .S3S2S1S0(ALU_SELECT), .Ai_1(ALU_Y[6]),
    .Ai_1_2(ALU_Y[7]), .out_7(AC_IN[7]), .Cout(alu1bit_8_cout));
  ALU1Bit alu1bit_9 (
    .Cin(alu1bit_8_cout), .Ai(ALU_Y[8]), .Bi(ALU_X[8]), .S3S2S1S0(ALU_SELECT), .Ai_1(ALU_Y[7]),
    .Ai_1_2(ALU_Y[8]), .out_7(AC_IN[8]), .Cout(alu1bit_9_cout));
  ALU1Bit alu1bit_10 (
    .Cin(alu1bit_9_cout), .Ai(ALU_Y[9]), .Bi(ALU_X[9]), .S3S2S1S0(ALU_SELECT), .Ai_1(ALU_Y[8]),
    .Ai_1_2(ALU_Y[9]), .out_7(AC_IN[9]), .Cout(alu1bit_10_cout));
  ALU1Bit alu1bit_11 (
    .Cin(alu1bit_10_cout), .Ai(ALU_Y[10]), .Bi(ALU_X[10]), .S3S2S1S0(ALU_SELECT), .Ai_1(ALU_Y[9]),
    .Ai_1_2(ALU_Y[10]), .out_7(AC_IN[10]), .Cout(alu1bit_11_cout));
  ALU1Bit alu1bit_12 (
    .Cin(alu1bit_11_cout), .Ai(ALU_Y[11]), .Bi(ALU_X[11]), .S3S2S1S0(ALU_SELECT), .Ai_1(ALU_Y[10]),
    .Ai_1_2(ALU_Y[11]), .out_7(AC_IN[11]), .Cout(alu1bit_12_cout));
  ALU1Bit alu1bit_13 (
    .Cin(alu1bit_12_cout), .Ai(ALU_Y[12]), .Bi(ALU_X[12]), .S3S2S1S0(ALU_SELECT), .Ai_1(ALU_Y[11]),
    .Ai_1_2(ALU_Y[12]), .out_7(AC_IN[12]), .Cout(alu1bit_13_cout));
  ALU1Bit alu1bit_14 (
    .Cin(alu1bit_13_cout), .Ai(ALU_Y[13]), .Bi(ALU_X[13]), .S3S2S1S0(ALU_SELECT), .Ai_1(ALU_Y[12]),
    .Ai_1_2(ALU_Y[13]), .out_7(AC_IN[13]), .Cout(alu1bit_14_cout));
  ALU1Bit alu1bit_15 (
    .Cin(alu1bit_14_cout), .Ai(ALU_Y[14]), .Bi(ALU_X[14]), .S3S2S1S0(ALU_SELECT), .Ai_1(ALU_Y[13]),
    .Ai_1_2(ALU_Y[14]), .out_7(AC_IN[14]), .Cout(alu1bit_15_cout));
  ALU1Bit alu1bit_16 (
    .Cin(alu1bit_15_cout), .Ai(ALU_Y[15]), .Bi(ALU_X[15]), .S3S2S1S0(ALU_SELECT), .Ai_1(ALU_Y[14]),
    .Ai_1_2(E), .out_7(AC_IN[15]), .Cout(alu1bit_16_cout));
  D_Flip_Flop u_R (.clk(CLOCK), .D(or_11_out), .Q(R));  // open: Qn, preset, en, reset
  and and_59 (and_59_out, R, not_9_out);
  not not_9 (not_9_out, T2);
  not not_10 (R_prime, R);
  // also tied to GND on the sheet: {multiplexer_1_out[8], multiplexer_1_out[9], multiplexer_1_out[10], multiplexer_1_out[11], multiplexer_1_out_2[0], multiplexer_1_out_2[1], multiplexer_1_out_2[2], multiplexer_1_out_2[3]}

  // Other names for the same wires on the sheet: IR[11:0] = {B11, B10, B9, B8, B7, B6, B5, B4, B3, B2, B1, B0};
  //   Opcode[2:0] = IR[14:12]

  // Notes on the sheet:
  //   BUS SYSTEM
  //   PC CONTROL
  //   AR CONTROL
  //   E CONTROL
  //   OUTR CONTROL
  //   IR CONTROL
  //   DR CONTROL
  //   RAM CONTROL
  //   TR CONTROL
  //   SEQUENCE TIMING
  //   SC CONTROL
  //   AC CONTROL
  //   INSTRUCTION FORMAT
  //   16 BIT ALU
endmodule

module ALU1Bit (
  input  Cin,
  input  Ai_1,
  input  Ai,
  input  Bi,
  input  [3:0] S3S2S1S0,
  input  Ai_1_2,
  output out_7,
  output Cout
);

  wire adder_1_out, and_1_out, multiplexer_1_out, multiplexer_2_out, not_1_out, not_2_out, not_3_out,
       or_1_out, xor_1_out;

  not not_1 (not_1_out, 1'b0);
  and and_1 (and_1_out, Ai, Bi);
  or or_1 (or_1_out, Ai, Bi);
  xor xor_1 (xor_1_out, Ai, Bi);
  not not_2 (not_2_out, Ai);
  not not_3 (not_3_out, Bi);
  Multiplexer #(.select(2), .enable("false")) multiplexer_1 (
    .in0(Bi), .in1(not_3_out), .in2(1'b0), .in3(not_1_out), .out(multiplexer_1_out), .sel(S3S2S1S0[1:0]));
  Adder #(.width(1)) adder_1 (.a(Ai), .b(multiplexer_1_out), .out(adder_1_out), .cin(Cin), .cout(Cout));
  Multiplexer #(.select(2), .enable("false")) multiplexer_2 (
    .in0(and_1_out), .in1(or_1_out), .in2(xor_1_out), .in3(not_2_out), .out(multiplexer_2_out),
    .sel(S3S2S1S0[1:0]));
  Multiplexer #(.select(2), .enable("false")) multiplexer_3 (
    .in0(adder_1_out), .in1(multiplexer_2_out), .in2(Ai_1), .in3(Ai_1_2), .out(out_7), .sel(S3S2S1S0[3:2]));

  // Notes on the sheet:
  //   Di
endmodule

module ALU (
  input  [15:0] B,
  input  [15:0] A,
  input  [4:0] F3F2F1F0CIN,
  input  EIN,
  output EOUT,
  output [15:0] S
);

  wire adder_1_cout, adder_1_out, adder_2_cout, adder_2_out, adder_3_cout, adder_3_out, adder_4_cout,
       adder_4_out, adder_5_cout, adder_5_out, adder_6_cout, adder_6_out, adder_7_cout, adder_7_out,
       adder_8_cout, adder_8_out, adder_9_cout, adder_9_out, adder_10_cout, adder_10_out, adder_11_cout,
       adder_11_out, adder_12_cout, adder_12_out, adder_13_cout, adder_13_out, adder_14_cout, adder_14_out,
       adder_15_cout, adder_15_out, adder_16_cout, adder_16_out, and_1_out, and_2_out, and_3_out, and_4_out,
       and_5_out, and_6_out, and_7_out, and_8_out, and_9_out, and_10_out, and_11_out, and_12_out, and_13_out,
       and_14_out, and_15_out, and_16_out, multiplexer_1_out, multiplexer_2_out, multiplexer_3_out,
       multiplexer_4_out, multiplexer_5_out, multiplexer_6_out, multiplexer_7_out, multiplexer_8_out,
       multiplexer_9_out, multiplexer_10_out, multiplexer_11_out, multiplexer_12_out, multiplexer_13_out,
       multiplexer_14_out, multiplexer_15_out, multiplexer_16_out, multiplexer_17_out, multiplexer_18_out,
       multiplexer_19_out, multiplexer_20_out, multiplexer_21_out, multiplexer_22_out, multiplexer_23_out,
       multiplexer_24_out, multiplexer_25_out, multiplexer_26_out, multiplexer_27_out, multiplexer_28_out,
       multiplexer_29_out, multiplexer_30_out, multiplexer_31_out, multiplexer_32_out, not_1_out, not_2_out,
       not_3_out, not_4_out, not_5_out, not_6_out, not_7_out, not_8_out, not_9_out, not_10_out, not_11_out,
       not_12_out, not_13_out, not_14_out, not_15_out, not_16_out, not_17_out, not_18_out, not_19_out,
       not_20_out, not_21_out, not_22_out, not_23_out, not_24_out, not_25_out, not_26_out, not_27_out,
       not_28_out, not_29_out, not_30_out, not_31_out, not_32_out, not_33_out, not_34_out, not_35_out,
       not_36_out, not_37_out, not_38_out, not_39_out, not_40_out, not_41_out, not_42_out, not_43_out,
       not_44_out, not_45_out, not_46_out, not_47_out, not_48_out, or_1_out, or_2_out, or_3_out, or_4_out,
       or_5_out, or_6_out, or_7_out, or_8_out, or_9_out, or_10_out, or_11_out, or_12_out, or_13_out,
       or_14_out, or_15_out, or_16_out, xor_1_out, xor_2_out, xor_3_out, xor_4_out, xor_5_out, xor_6_out,
       xor_7_out, xor_8_out, xor_9_out, xor_10_out, xor_11_out, xor_12_out, xor_13_out, xor_14_out,
       xor_15_out, xor_16_out;

  // Probe on B
  // Probe on A
  not not_1 (not_1_out, 1'b0);
  not not_2 (not_2_out, A[0]);
  not not_3 (not_3_out, 1'b0);
  not not_4 (not_4_out, A[1]);
  not not_5 (not_5_out, 1'b0);
  not not_6 (not_6_out, A[2]);
  not not_7 (not_7_out, 1'b0);
  not not_8 (not_8_out, A[3]);
  not not_9 (not_9_out, 1'b0);
  not not_10 (not_10_out, A[4]);
  not not_11 (not_11_out, 1'b0);
  not not_12 (not_12_out, A[5]);
  not not_13 (not_13_out, 1'b0);
  not not_14 (not_14_out, A[6]);
  not not_15 (not_15_out, 1'b0);
  not not_16 (not_16_out, A[7]);
  not not_17 (not_17_out, B[0]);
  and and_1 (and_1_out, A[0], B[0]);
  or or_1 (or_1_out, A[0], B[0]);
  xor xor_1 (xor_1_out, A[0], B[0]);
  not not_18 (not_18_out, B[1]);
  and and_2 (and_2_out, A[1], B[1]);
  or or_2 (or_2_out, A[1], B[1]);
  xor xor_2 (xor_2_out, A[1], B[1]);
  not not_19 (not_19_out, B[2]);
  and and_3 (and_3_out, A[2], B[2]);
  or or_3 (or_3_out, A[2], B[2]);
  xor xor_3 (xor_3_out, A[2], B[2]);
  not not_20 (not_20_out, B[3]);
  and and_4 (and_4_out, A[3], B[3]);
  or or_4 (or_4_out, A[3], B[3]);
  xor xor_4 (xor_4_out, A[3], B[3]);
  not not_21 (not_21_out, B[4]);
  and and_5 (and_5_out, A[4], B[4]);
  or or_5 (or_5_out, A[4], B[4]);
  xor xor_5 (xor_5_out, A[4], B[4]);
  not not_22 (not_22_out, B[5]);
  and and_6 (and_6_out, A[5], B[5]);
  or or_6 (or_6_out, A[5], B[5]);
  xor xor_6 (xor_6_out, A[5], B[5]);
  not not_23 (not_23_out, B[6]);
  and and_7 (and_7_out, A[6], B[6]);
  or or_7 (or_7_out, A[6], B[6]);
  xor xor_7 (xor_7_out, A[6], B[6]);
  not not_24 (not_24_out, B[7]);
  and and_8 (and_8_out, A[7], B[7]);
  or or_8 (or_8_out, A[7], B[7]);
  xor xor_8 (xor_8_out, A[7], B[7]);
  not not_25 (not_25_out, B[8]);
  not not_26 (not_26_out, 1'b0);
  and and_9 (and_9_out, A[8], B[8]);
  or or_9 (or_9_out, A[8], B[8]);
  xor xor_9 (xor_9_out, A[8], B[8]);
  not not_27 (not_27_out, A[8]);
  not not_28 (not_28_out, B[9]);
  not not_29 (not_29_out, 1'b0);
  and and_10 (and_10_out, A[9], B[9]);
  or or_10 (or_10_out, A[9], B[9]);
  xor xor_10 (xor_10_out, A[9], B[9]);
  not not_30 (not_30_out, A[9]);
  not not_31 (not_31_out, B[10]);
  not not_32 (not_32_out, 1'b0);
  and and_11 (and_11_out, A[10], B[10]);
  or or_11 (or_11_out, A[10], B[10]);
  xor xor_11 (xor_11_out, A[10], B[10]);
  not not_33 (not_33_out, A[10]);
  not not_34 (not_34_out, B[11]);
  not not_35 (not_35_out, 1'b0);
  and and_12 (and_12_out, A[11], B[11]);
  or or_12 (or_12_out, A[11], B[11]);
  xor xor_12 (xor_12_out, A[11], B[11]);
  not not_36 (not_36_out, A[11]);
  not not_37 (not_37_out, B[12]);
  not not_38 (not_38_out, 1'b0);
  and and_13 (and_13_out, A[12], B[12]);
  or or_13 (or_13_out, A[12], B[12]);
  xor xor_13 (xor_13_out, A[12], B[12]);
  not not_39 (not_39_out, A[12]);
  not not_40 (not_40_out, B[13]);
  not not_41 (not_41_out, 1'b0);
  and and_14 (and_14_out, A[13], B[13]);
  or or_14 (or_14_out, A[13], B[13]);
  xor xor_14 (xor_14_out, A[13], B[13]);
  not not_42 (not_42_out, A[13]);
  not not_43 (not_43_out, B[14]);
  not not_44 (not_44_out, 1'b0);
  and and_15 (and_15_out, A[14], B[14]);
  or or_15 (or_15_out, A[14], B[14]);
  xor xor_15 (xor_15_out, A[14], B[14]);
  not not_45 (not_45_out, A[14]);
  not not_46 (not_46_out, B[15]);
  not not_47 (not_47_out, 1'b0);
  and and_16 (and_16_out, A[15], B[15]);
  or or_16 (or_16_out, A[15], B[15]);
  xor xor_16 (xor_16_out, A[15], B[15]);
  not not_48 (not_48_out, A[15]);
  Multiplexer #(.select(2), .enable("false")) multiplexer_1 (
    .in0(B[0]), .in1(not_17_out), .in2(1'b0), .in3(not_1_out), .out(multiplexer_1_out), .sel(F3F2F1F0CIN[2:1]));
  Multiplexer #(.select(2), .enable("false")) multiplexer_2 (
    .in0(B[1]), .in1(not_18_out), .in2(1'b0), .in3(not_3_out), .out(multiplexer_2_out), .sel(F3F2F1F0CIN[2:1]));
  Multiplexer #(.select(2), .enable("false")) multiplexer_3 (
    .in0(B[2]), .in1(not_19_out), .in2(1'b0), .in3(not_5_out), .out(multiplexer_3_out), .sel(F3F2F1F0CIN[2:1]));
  Multiplexer #(.select(2), .enable("false")) multiplexer_4 (
    .in0(B[3]), .in1(not_20_out), .in2(1'b0), .in3(not_7_out), .out(multiplexer_4_out), .sel(F3F2F1F0CIN[2:1]));
  Multiplexer #(.select(2), .enable("false")) multiplexer_5 (
    .in0(B[4]), .in1(not_21_out), .in2(1'b0), .in3(not_9_out), .out(multiplexer_5_out), .sel(F3F2F1F0CIN[2:1]));
  Multiplexer #(.select(2), .enable("false")) multiplexer_6 (
    .in0(B[5]), .in1(not_22_out), .in2(1'b0), .in3(not_11_out), .out(multiplexer_6_out),
    .sel(F3F2F1F0CIN[2:1]));
  Multiplexer #(.select(2), .enable("false")) multiplexer_7 (
    .in0(B[6]), .in1(not_23_out), .in2(1'b0), .in3(not_13_out), .out(multiplexer_7_out),
    .sel(F3F2F1F0CIN[2:1]));
  Multiplexer #(.select(2), .enable("false")) multiplexer_8 (
    .in0(B[7]), .in1(not_24_out), .in2(1'b0), .in3(not_15_out), .out(multiplexer_8_out),
    .sel(F3F2F1F0CIN[2:1]));
  Multiplexer #(.select(2), .enable("false")) multiplexer_9 (
    .in0(B[8]), .in1(not_25_out), .in2(1'b0), .in3(not_26_out), .out(multiplexer_9_out),
    .sel(F3F2F1F0CIN[2:1]));
  Multiplexer #(.select(2), .enable("false")) multiplexer_10 (
    .in0(B[9]), .in1(not_28_out), .in2(1'b0), .in3(not_29_out), .out(multiplexer_10_out),
    .sel(F3F2F1F0CIN[2:1]));
  Multiplexer #(.select(2), .enable("false")) multiplexer_11 (
    .in0(B[10]), .in1(not_31_out), .in2(1'b0), .in3(not_32_out), .out(multiplexer_11_out),
    .sel(F3F2F1F0CIN[2:1]));
  Multiplexer #(.select(2), .enable("false")) multiplexer_12 (
    .in0(B[11]), .in1(not_34_out), .in2(1'b0), .in3(not_35_out), .out(multiplexer_12_out),
    .sel(F3F2F1F0CIN[2:1]));
  Multiplexer #(.select(2), .enable("false")) multiplexer_13 (
    .in0(B[12]), .in1(not_37_out), .in2(1'b0), .in3(not_38_out), .out(multiplexer_13_out),
    .sel(F3F2F1F0CIN[2:1]));
  Multiplexer #(.select(2), .enable("false")) multiplexer_14 (
    .in0(B[13]), .in1(not_40_out), .in2(1'b0), .in3(not_41_out), .out(multiplexer_14_out),
    .sel(F3F2F1F0CIN[2:1]));
  Multiplexer #(.select(2), .enable("false")) multiplexer_15 (
    .in0(B[14]), .in1(not_43_out), .in2(1'b0), .in3(not_44_out), .out(multiplexer_15_out),
    .sel(F3F2F1F0CIN[2:1]));
  Multiplexer #(.select(2), .enable("false")) multiplexer_16 (
    .in0(B[15]), .in1(not_46_out), .in2(1'b0), .in3(not_47_out), .out(multiplexer_16_out),
    .sel(F3F2F1F0CIN[2:1]));
  Multiplexer #(.select(2), .enable("false")) multiplexer_17 (
    .in0(and_1_out), .in1(or_1_out), .in2(xor_1_out), .in3(not_2_out), .out(multiplexer_17_out),
    .sel(F3F2F1F0CIN[2:1]));
  Multiplexer #(.select(2), .enable("false")) multiplexer_18 (
    .in0(and_2_out), .in1(or_2_out), .in2(xor_2_out), .in3(not_4_out), .out(multiplexer_18_out),
    .sel(F3F2F1F0CIN[2:1]));
  Multiplexer #(.select(2), .enable("false")) multiplexer_19 (
    .in0(and_3_out), .in1(or_3_out), .in2(xor_3_out), .in3(not_6_out), .out(multiplexer_19_out),
    .sel(F3F2F1F0CIN[2:1]));
  Multiplexer #(.select(2), .enable("false")) multiplexer_20 (
    .in0(and_4_out), .in1(or_4_out), .in2(xor_4_out), .in3(not_8_out), .out(multiplexer_20_out),
    .sel(F3F2F1F0CIN[2:1]));
  Multiplexer #(.select(2), .enable("false")) multiplexer_21 (
    .in0(and_5_out), .in1(or_5_out), .in2(xor_5_out), .in3(not_10_out), .out(multiplexer_21_out),
    .sel(F3F2F1F0CIN[2:1]));
  Multiplexer #(.select(2), .enable("false")) multiplexer_22 (
    .in0(and_6_out), .in1(or_6_out), .in2(xor_6_out), .in3(not_12_out), .out(multiplexer_22_out),
    .sel(F3F2F1F0CIN[2:1]));
  Multiplexer #(.select(2), .enable("false")) multiplexer_23 (
    .in0(and_7_out), .in1(or_7_out), .in2(xor_7_out), .in3(not_14_out), .out(multiplexer_23_out),
    .sel(F3F2F1F0CIN[2:1]));
  Multiplexer #(.select(2), .enable("false")) multiplexer_24 (
    .in0(and_8_out), .in1(or_8_out), .in2(xor_8_out), .in3(not_16_out), .out(multiplexer_24_out),
    .sel(F3F2F1F0CIN[2:1]));
  Multiplexer #(.select(2), .enable("false")) multiplexer_25 (
    .in0(and_9_out), .in1(or_9_out), .in2(xor_9_out), .in3(not_27_out), .out(multiplexer_25_out),
    .sel(F3F2F1F0CIN[2:1]));
  Multiplexer #(.select(2), .enable("false")) multiplexer_26 (
    .in0(and_10_out), .in1(or_10_out), .in2(xor_10_out), .in3(not_30_out), .out(multiplexer_26_out),
    .sel(F3F2F1F0CIN[2:1]));
  Multiplexer #(.select(2), .enable("false")) multiplexer_27 (
    .in0(and_11_out), .in1(or_11_out), .in2(xor_11_out), .in3(not_33_out), .out(multiplexer_27_out),
    .sel(F3F2F1F0CIN[2:1]));
  Multiplexer #(.select(2), .enable("false")) multiplexer_28 (
    .in0(and_12_out), .in1(or_12_out), .in2(xor_12_out), .in3(not_36_out), .out(multiplexer_28_out),
    .sel(F3F2F1F0CIN[2:1]));
  Multiplexer #(.select(2), .enable("false")) multiplexer_29 (
    .in0(and_13_out), .in1(or_13_out), .in2(xor_13_out), .in3(not_39_out), .out(multiplexer_29_out),
    .sel(F3F2F1F0CIN[2:1]));
  Multiplexer #(.select(2), .enable("false")) multiplexer_30 (
    .in0(and_14_out), .in1(or_14_out), .in2(xor_14_out), .in3(not_42_out), .out(multiplexer_30_out),
    .sel(F3F2F1F0CIN[2:1]));
  Multiplexer #(.select(2), .enable("false")) multiplexer_31 (
    .in0(and_15_out), .in1(or_15_out), .in2(xor_15_out), .in3(not_45_out), .out(multiplexer_31_out),
    .sel(F3F2F1F0CIN[2:1]));
  Multiplexer #(.select(2), .enable("false")) multiplexer_32 (
    .in0(and_16_out), .in1(or_16_out), .in2(xor_16_out), .in3(not_48_out), .out(multiplexer_32_out),
    .sel(F3F2F1F0CIN[2:1]));
  Adder #(.width(1)) adder_1 (
    .a(A[0]), .b(multiplexer_1_out), .out(adder_1_out), .cin(F3F2F1F0CIN[0]), .cout(adder_1_cout));
  Adder #(.width(1)) adder_2 (
    .a(A[1]), .b(multiplexer_2_out), .out(adder_2_out), .cin(adder_1_cout), .cout(adder_2_cout));
  Adder #(.width(1)) adder_3 (
    .a(A[2]), .b(multiplexer_3_out), .out(adder_3_out), .cin(adder_2_cout), .cout(adder_3_cout));
  Adder #(.width(1)) adder_4 (
    .a(A[3]), .b(multiplexer_4_out), .out(adder_4_out), .cin(adder_3_cout), .cout(adder_4_cout));
  Adder #(.width(1)) adder_5 (
    .a(A[4]), .b(multiplexer_5_out), .out(adder_5_out), .cin(adder_4_cout), .cout(adder_5_cout));
  Adder #(.width(1)) adder_6 (
    .a(A[5]), .b(multiplexer_6_out), .out(adder_6_out), .cin(adder_5_cout), .cout(adder_6_cout));
  Adder #(.width(1)) adder_7 (
    .a(A[6]), .b(multiplexer_7_out), .out(adder_7_out), .cin(adder_6_cout), .cout(adder_7_cout));
  Adder #(.width(1)) adder_8 (
    .a(A[7]), .b(multiplexer_8_out), .out(adder_8_out), .cin(adder_7_cout), .cout(adder_8_cout));
  Adder #(.width(1)) adder_9 (
    .a(A[8]), .b(multiplexer_9_out), .out(adder_9_out), .cin(adder_8_cout), .cout(adder_9_cout));
  Adder #(.width(1)) adder_10 (
    .a(A[9]), .b(multiplexer_10_out), .out(adder_10_out), .cin(adder_9_cout), .cout(adder_10_cout));
  Adder #(.width(1)) adder_11 (
    .a(A[10]), .b(multiplexer_11_out), .out(adder_11_out), .cin(adder_10_cout), .cout(adder_11_cout));
  Adder #(.width(1)) adder_12 (
    .a(A[11]), .b(multiplexer_12_out), .out(adder_12_out), .cin(adder_11_cout), .cout(adder_12_cout));
  Adder #(.width(1)) adder_13 (
    .a(A[12]), .b(multiplexer_13_out), .out(adder_13_out), .cin(adder_12_cout), .cout(adder_13_cout));
  Adder #(.width(1)) adder_14 (
    .a(A[13]), .b(multiplexer_14_out), .out(adder_14_out), .cin(adder_13_cout), .cout(adder_14_cout));
  Adder #(.width(1)) adder_15 (
    .a(A[14]), .b(multiplexer_15_out), .out(adder_15_out), .cin(adder_14_cout), .cout(adder_15_cout));
  Adder #(.width(1)) adder_16 (
    .a(A[15]), .b(multiplexer_16_out), .out(adder_16_out), .cin(adder_15_cout), .cout(adder_16_cout));
  Multiplexer #(.select(2), .enable("false")) multiplexer_33 (
    .in0(adder_16_cout), .in1(adder_16_cout), .in2(A[15]), .in3(A[0]), .out(EOUT), .sel(F3F2F1F0CIN[4:3]));
  Multiplexer #(.select(2), .enable("false")) multiplexer_34 (
    .in0(adder_1_out), .in1(multiplexer_17_out), .in2(EIN), .in3(A[1]), .out(S[0]), .sel(F3F2F1F0CIN[4:3]));
  Multiplexer #(.select(2), .enable("false")) multiplexer_35 (
    .in0(adder_2_out), .in1(multiplexer_18_out), .in2(A[0]), .in3(A[2]), .out(S[1]), .sel(F3F2F1F0CIN[4:3]));
  Multiplexer #(.select(2), .enable("false")) multiplexer_36 (
    .in0(adder_3_out), .in1(multiplexer_19_out), .in2(A[1]), .in3(A[3]), .out(S[2]), .sel(F3F2F1F0CIN[4:3]));
  Multiplexer #(.select(2), .enable("false")) multiplexer_37 (
    .in0(adder_4_out), .in1(multiplexer_20_out), .in2(A[2]), .in3(A[4]), .out(S[3]), .sel(F3F2F1F0CIN[4:3]));
  Multiplexer #(.select(2), .enable("false")) multiplexer_38 (
    .in0(adder_5_out), .in1(multiplexer_21_out), .in2(A[3]), .in3(A[5]), .out(S[4]), .sel(F3F2F1F0CIN[4:3]));
  Multiplexer #(.select(2), .enable("false")) multiplexer_39 (
    .in0(adder_6_out), .in1(multiplexer_22_out), .in2(A[4]), .in3(A[6]), .out(S[5]), .sel(F3F2F1F0CIN[4:3]));
  Multiplexer #(.select(2), .enable("false")) multiplexer_40 (
    .in0(adder_7_out), .in1(multiplexer_23_out), .in2(A[5]), .in3(A[7]), .out(S[6]), .sel(F3F2F1F0CIN[4:3]));
  Multiplexer #(.select(2), .enable("false")) multiplexer_41 (
    .in0(adder_8_out), .in1(multiplexer_24_out), .in2(A[6]), .in3(A[8]), .out(S[7]), .sel(F3F2F1F0CIN[4:3]));
  Multiplexer #(.select(2), .enable("false")) multiplexer_42 (
    .in0(adder_9_out), .in1(multiplexer_25_out), .in2(A[7]), .in3(A[9]), .out(S[8]), .sel(F3F2F1F0CIN[4:3]));
  Multiplexer #(.select(2), .enable("false")) multiplexer_43 (
    .in0(adder_10_out), .in1(multiplexer_26_out), .in2(A[8]), .in3(A[10]), .out(S[9]), .sel(F3F2F1F0CIN[4:3]));
  Multiplexer #(.select(2), .enable("false")) multiplexer_44 (
    .in0(adder_11_out), .in1(multiplexer_27_out), .in2(A[9]), .in3(A[11]), .out(S[10]), .sel(F3F2F1F0CIN[4:3]));
  Multiplexer #(.select(2), .enable("false")) multiplexer_45 (
    .in0(adder_12_out), .in1(multiplexer_28_out), .in2(A[10]), .in3(A[12]), .out(S[11]),
    .sel(F3F2F1F0CIN[4:3]));
  Multiplexer #(.select(2), .enable("false")) multiplexer_46 (
    .in0(adder_13_out), .in1(multiplexer_29_out), .in2(A[11]), .in3(A[13]), .out(S[12]),
    .sel(F3F2F1F0CIN[4:3]));
  Multiplexer #(.select(2), .enable("false")) multiplexer_47 (
    .in0(adder_14_out), .in1(multiplexer_30_out), .in2(A[12]), .in3(A[14]), .out(S[13]),
    .sel(F3F2F1F0CIN[4:3]));
  Multiplexer #(.select(2), .enable("false")) multiplexer_48 (
    .in0(adder_15_out), .in1(multiplexer_31_out), .in2(A[13]), .in3(A[15]), .out(S[14]),
    .sel(F3F2F1F0CIN[4:3]));
  Multiplexer #(.select(2), .enable("false")) multiplexer_49 (
    .in0(adder_16_out), .in1(multiplexer_32_out), .in2(A[14]), .in3(EIN), .out(S[15]), .sel(F3F2F1F0CIN[4:3]));

  // Notes on the sheet:
  //   Di
  //   Di
  //   Di
  //   Di
  //   Di
  //   Di
  //   Di
  //   Di
  //   Di
  //   Di
  //   Di
  //   Di
  //   Di
  //   Di
  //   Di
  //   Di
endmodule

module REG16BIT (
  input  [15:0] D,
  input  LD,
  input  INC,
  input  CLK,
  input  CLR,
  output [15:0] Q
);

  wire [15:0] adder_1_out, multiplexer_1_out;

  Multiplexer #(.width(16), .enable("false")) multiplexer_1 (
    .in0(D), .in1(adder_1_out), .out(multiplexer_1_out), .sel(INC));
  Register #(.width(16)) register_1 (.D(multiplexer_1_out), .en(LD), .Q(Q), .clk(CLK), .clr(CLR));
  Adder #(.width(16)) adder_1 (.a(Q), .b(16'h1), .out(adder_1_out), .cin(1'b0));  // open: cout
endmodule

module REG8BIT (
  input  [7:0] D,
  input  LD,
  input  INC,
  input  CLK,
  input  CLR,
  output [7:0] Q
);

  wire [7:0] adder_1_out, multiplexer_1_out;

  Multiplexer #(.width(8), .enable("false")) multiplexer_1 (
    .in0(D), .in1(adder_1_out), .out(multiplexer_1_out), .sel(INC));
  Register register_1 (.D(multiplexer_1_out), .en(LD), .Q(Q), .clk(CLK), .clr(CLR));
  Adder adder_1 (.a(Q), .b(8'h1), .out(adder_1_out), .cin(1'b0));  // open: cout
endmodule

module REG12BIT (
  input  [11:0] D,
  input  LD,
  input  INC,
  input  CLK,
  input  CLR,
  output [11:0] Q
);

  wire [11:0] adder_1_out, multiplexer_1_out;

  Multiplexer #(.width(12), .enable("false")) multiplexer_1 (
    .in0(D), .in1(adder_1_out), .out(multiplexer_1_out), .sel(INC));
  Register #(.width(12)) register_1 (.D(multiplexer_1_out), .en(LD), .Q(Q), .clk(CLK), .clr(CLR));
  Adder #(.width(12)) adder_1 (.a(Q), .b(12'h1), .out(adder_1_out), .cin(1'b0));  // open: cout
endmodule
