// Logisim project Full_Adder_From_Half_adder.circ as structural Verilog: 2 circuits, main circuit main
module main (
  input  A,
  input  Cin,
  input  B,
  output Sum,
  output Cout
);

  wire half_adder_1_cout, half_adder_1_sum, half_adder_2_cout;

  half_adder half_adder_1 (.A(A), .B(B), .Sum(half_adder_1_sum), .Cout(half_adder_1_cout));
  xor xor_1 (Cout, half_adder_1_cout, half_adder_2_cout);
  half_adder half_adder_2 (.A(half_adder_1_sum), .B(Cin), .Sum(Sum), .Cout(half_adder_2_cout));
endmodule

module half_adder (
  input  A,
  input  B,
  output Sum,
  output Cout
);

  xor xor_1 (Sum, A, B);
  and and_1 (Cout, A, B);
endmodule
