// Logisim project 2_bit_arithmetic_circuit.circ as structural Verilog: 1 circuit, main circuit main
module main (
  input  Cin,
  input  S1,
  input  S0,
  input  A0,
  input  B0,
  input  Bit__0,
  input  A1,
  input  B1,
  input  Enable,
  output D0,
  output D1,
  output Cout
);

  wire adder_1_cout, multiplexer_1_out, multiplexer_2_out, not_1_out, not_2_out, not_3_out;

  not not_1 (not_1_out, B0);
  not not_2 (not_2_out, Bit__0);
  not not_3 (not_3_out, B1);
  Multiplexer #(.select(2)) multiplexer_1 (
    .in0(B0), .in1(not_1_out), .in2(Bit__0), .in3(not_2_out), .out(multiplexer_1_out), .sel({S1, S0}),
    .en(Enable));
  Multiplexer #(.select(2)) multiplexer_2 (
    .in0(B1), .in1(not_3_out), .in2(Bit__0), .in3(not_2_out), .out(multiplexer_2_out), .sel({S1, S0}),
    .en(Enable));
  Adder #(.width(1)) adder_1 (.a(A0), .b(multiplexer_1_out), .out(D0), .cin(Cin), .cout(adder_1_cout));
  Adder #(.width(1)) adder_2 (.a(A1), .b(multiplexer_2_out), .out(D1), .cin(adder_1_cout), .cout(Cout));
endmodule
