// Logisim project 4_bit_BCD_subtractor.circ as structural Verilog: 1 circuit, main circuit main
module main (
  input  C0,
  input  x3_x2_x1_x0,
  input  [3:0] A3_A2_A1_A0,
  input  [3:0] B3B2B1B0,
  input  Bit__0,
  input  Bit__1,
  input  Bit__0_2,
  input  [3:0] in_8,
  output [3:0] out_9,
  output [3:0] out_10,
  output out_11,
  output out_12,
  output Output_Carry,
  output [3:0] out_14,
  output Cout,
  output [3:0] out_16
);

  wire adder_2_cout, and_1_out, and_2_out;
  wire [3:0] not_1_out;

  assign not_1_out = ~B3B2B1B0;  // NOT_Gate not_1, 4 bits wide
  or or_1 (Output_Carry, adder_2_cout, and_1_out, and_2_out);
  Adder #(.width(4)) adder_1 (
    .a(not_1_out), .b({Bit__1, Bit__0, Bit__1, Bit__0}), .out(out_9), .cin(x3_x2_x1_x0), .cout(out_11));
  and and_1 (and_1_out, out_10[3], out_10[2]);
  and and_2 (and_2_out, out_10[3], out_10[1]);
  Adder #(.width(4)) adder_2 (.a(A3_A2_A1_A0), .b(out_9), .out(out_10), .cin(C0), .cout(adder_2_cout));
  Adder #(.width(4)) adder_3 (
    .a(out_10), .b({Bit__0_2, {2{Output_Carry}}, Bit__0_2}), .out(out_14), .cout(Cout));  // open: cin
  Adder #(.width(4)) adder_4 (.a(out_14), .b(in_8), .out(out_16));  // open: cin, cout

  assign out_12 = out_10[0];

  // Notes on the sheet:
  //   Subtrahend
  //   Minimend
endmodule
