// Logisim project Arithmetic_circuit_1 bit.circ as structural Verilog: 1 circuit, main circuit main
// Bi
module main (
  input  Cin,
  input  Bi,
  input  Ai,
  input  [1:0] Select_Lines,
  output Di,
  output Cout
);

  wire multiplexer_1_out, not_1_out, not_2_out;

  not not_1 (not_1_out, Bi);
  not not_2 (not_2_out, 1'b0);
  Multiplexer #(.select(2), .enable("false")) multiplexer_1 (
    .in0(Bi), .in1(not_1_out), .in2(1'b0), .in3(not_2_out), .out(multiplexer_1_out), .sel(Select_Lines));
  Adder #(.width(1)) adder_1 (.a(Ai), .b(multiplexer_1_out), .out(Di), .cin(Cin), .cout(Cout));
endmodule
