// Logisim project Arithmetic_logic_shift_circuit.circ as structural Verilog: 1 circuit, main circuit main
module main (
  input  Cin,
  input  Ai,
  input  Bi,
  input  [3:0] S3S2S1S0,
  input  Ai_1,
  input  Ai_1_2,
  output out_7
);

  wire adder_1_out, and_1_out, multiplexer_1_out, multiplexer_2_out, not_1_out, not_2_out, not_3_out,
       or_1_out, xor_1_out;

  not not_1 (not_1_out, 1'b0);
  and and_1 (and_1_out, Ai, Bi);
  or or_1 (or_1_out, Ai, Bi);
  xor xor_1 (xor_1_out, Ai, Bi);
  not not_2 (not_2_out, Ai);
  not not_3 (not_3_out, Bi);
  Multiplexer #(.select(2), .enable("false")) multiplexer_1 (
    .in0(Bi), .in1(not_3_out), .in2(1'b0), .in3(not_1_out), .out(multiplexer_1_out), .sel(S3S2S1S0[1:0]));
  Adder #(.width(1)) adder_1 (.a(Ai), .b(multiplexer_1_out), .out(adder_1_out), .cin(Cin));  // open: cout
  Multiplexer #(.select(2), .enable("false")) multiplexer_2 (
    .in0(and_1_out), .in1(or_1_out), .in2(xor_1_out), .in3(not_2_out), .out(multiplexer_2_out),
    .sel(S3S2S1S0[1:0]));
  Multiplexer #(.select(2), .enable("false")) multiplexer_3 (
    .in0(adder_1_out), .in1(multiplexer_2_out), .in2(Ai_1), .in3(Ai_1_2), .out(out_7), .sel(S3S2S1S0[3:2]));

  // Notes on the sheet:
  //   shr
  //   shl
  //   Di
endmodule
