// Logisim project Basic Computer.circ as structural Verilog: 10 circuits, main circuit main
module main (
);

  wire AC_CLR, AC_INC, AC_LD, alu1bit_1_cout, alu1bit_2_cout, alu1bit_3_cout, alu1bit_4_cout, alu1bit_5_cout,
       alu1bit_6_cout, alu1bit_7_cout, alu1bit_8_cout, alu1bit_9_cout, alu1bit_10_cout, alu1bit_11_cout,
       alu1bit_12_cout, alu1bit_13_cout, alu1bit_14_cout, alu1bit_15_cout, alu1bit_16_cout, ALU_CIN,
       and_1_out, and_4_out, and_5_out, and_6_out, and_8_out, and_9_out, and_10_out, and_11_out, and_12_out,
       and_13_out, and_14_out, and_15_out, and_16_out, and_17_out, and_18_out, and_19_out, and_20_out,
       and_21_out, and_22_out, and_23_out, and_24_out, and_25_out, and_26_out, and_27_out, and_28_out,
       and_29_out, and_31_out, and_32_out, and_33_out, and_35_out, and_36_out, and_37_out, and_38_out,
       and_39_out, and_40_out, and_41_out, and_42_out, and_43_out, and_44_out, and_47_out, and_48_out,
       and_49_out, and_50_out, and_51_out, and_54_out, and_55_out, and_56_out, and_57_out, and_58_out,
       and_59_out, and_60_out, and_63_out, and_64_out, and_65_out, and_66_out, and_67_out, and_68_out,
       and_69_out, and_70_out, and_71_out, and_72_out, and_73_out, and_74_out, and_75_out, and_76_out,
       and_77_out, and_78_out, and_79_out, and_80_out, and_81_out, and_82_out, and_83_out, and_84_out,
       and_85_out, and_86_out, and_87_out, and_88_out, and_89_out, and_90_out, and_91_out, and_92_out,
       and_93_out, and_94_out, and_95_out, and_96_out, and_97_out, and_98_out, AR_CLR, AR_INC, AR_LD, CLOCK,
       clock_1_out, comparator_1_eq, comparator_2_eq, D0, D1, D2, D3, D4, D5, D6, D7, DR_INC, DR_LD, E, E_LD,
       EIN, enc1bit_1_out_3, FGI, FGO, I, IEN_q, IR_LD, not_1_out, not_2_out, not_3_out, not_4_out,
       not_5_out, not_6_out, not_7_out, not_8_out, not_9_out, not_10_out, not_11_out, not_12_out, not_13_out,
       or_4_out, or_5_out, or_6_out, or_7_out, or_11_out, or_12_out, or_13_out, or_15_out, or_17_out,
       or_18_out, or_19_out, or_20_out, or_21_out, or_22_out, OUTR_LD, p, PC_CLR, PC_INC, PC_LD, R, R_prime,
       r_t, RAM_LD, S_qn, SC_CLR, T0, T1, T2, T3, T4, T5, T6, T7, T8, T9, T10, T11, T12, T13, T14, T15, TR_LD;
  wire [1:0] enc2bit_1_out_5;
  wire [2:0] BUS_SELECT, E_SELECT;
  wire [3:0] ALU_SELECT, T;
  wire [7:0] INPR;
  wire [11:0] AR, B, PC;
  wire [15:0] AC, AC_IN, ALU_X, ALU_Y, bit_extender_1_out, BUS, DR, ram_1_data, TR_q;
  wire [15:12] IR;

  and and_1 (and_1_out, r_t, B[0]);
  // Probe on BUS
  // Probe on AR
  // Probe on PC
  // Probe on DR
  // Probe on {IR, B}
  D_Flip_Flop S (.clk(CLOCK), .D(and_1_out), .Qn(S_qn), .en(S_qn));  // open: Q, preset, reset
  Comparator #(.width(16)) comparator_1 (.a(DR), .b({16{1'b0}}), .eq(comparator_1_eq));  // open: gt, lt
  Comparator #(.width(16)) comparator_2 (.a(AC), .b({16{1'b0}}), .eq(comparator_2_eq));  // open: gt, lt
  REG12BIT u_AR (.D(BUS[11:0]), .INC(AR_INC), .CLK(CLOCK), .CLR(AR_CLR), .Q(AR), .LD(AR_LD));
  REG12BIT u_PC (.D(BUS[11:0]), .INC(PC_INC), .CLK(CLOCK), .CLR(PC_CLR), .Q(PC), .LD(PC_LD));
  REG16BIT u_AC (.D(AC_IN), .Q(AC), .CLK(CLOCK), .CLR(AC_CLR), .LD(AC_LD), .INC(AC_INC));
  REG16BIT u_DR (.D(BUS), .Q(DR), .CLK(CLOCK), .CLR(1'b0), .LD(DR_LD), .INC(DR_INC));
  REG16BIT u_IR (.D(BUS), .Q({IR, B}), .CLK(CLOCK), .CLR(1'b0), .LD(IR_LD), .INC(1'b0));
  REG16BIT TR (.D(BUS), .Q(TR_q), .CLK(CLOCK), .CLR(1'b0), .LD(TR_LD), .INC(1'b0));
  REG8BIT OUTR (.D(BUS[7:0]), .CLK(CLOCK), .CLR(1'b0), .LD(OUTR_LD), .INC(1'b0));  // open: Q
  assign CLOCK = S_qn ? clock_1_out : 1'bz;  // Controlled_Buffer controlled_buffer_1
  Clock clock_1 (.out(clock_1_out));
  not not_1 (not_1_out, D7);
  not not_2 (not_2_out, AC[15]);
  not not_3 (not_3_out, E);
  not not_4 (not_4_out, FGO);
  // Probe on AR
  // Probe on PC
  // Probe on AC
  // Probe on DR
  // Probe on {IR, B}
  // Probe on TR_q
  RAM #(.addrWidth(12), .dataWidth(16), .bus("separate")) ram_1 (
    .addr(AR), .din(BUS), .data(ram_1_data), .str(RAM_LD), .clk(CLOCK));  // open: sel, ld, clr
  // Probe on ram_1_data
  // Probe on AC
  // Probe on ALU_SELECT
  // Probe on ALU_CIN
  // Probe on AC_IN
  // Probe on ALU_X
  // Probe on ALU_Y
  and and_2 (AR_CLR, R, T0);
  and and_3 (AR_INC, D5, T4);
  and and_4 (and_4_out, R_prime, T2);
  and and_5 (and_5_out, not_1_out, I, T3);
  and and_6 (and_6_out, R_prime, T0);
  and and_7 (PC_CLR, R, T1);
  and and_8 (and_8_out, D4, T4);
  and and_9 (and_9_out, D5, T5);
  and and_10 (and_10_out, R_prime, T1);
  and and_11 (and_11_out, R, T2);
  and and_12 (and_12_out, r_t, AC[15], B[3]);
  and and_13 (and_13_out, D6, comparator_1_eq, T6);
  and and_14 (and_14_out, r_t, not_2_out, B[4]);
  and and_15 (and_15_out, r_t, comparator_2_eq, B[4]);
  and and_16 (and_16_out, r_t, not_3_out, B[4]);
  and and_17 (and_17_out, p, FGI, B[9]);
  and and_18 (and_18_out, p, not_4_out, B[8]);
  Multiplexer #(.select(3), .width(16), .enable("false")) multiplexer_1 (
    .in1({4'b0000, AR}), .in2({4'b0000, PC}), .in3(DR), .in4(AC), .in5({IR, B}), .in6(TR_q),
    .in7(ram_1_data), .out(BUS), .sel(BUS_SELECT));  // open: in0
  or or_1 (AR_LD, and_4_out, and_5_out, and_6_out);
  or or_2 (PC_LD, and_8_out, and_9_out);
  // Probe on B
  // Probe on r_t
  // Probe on p
  // Probe on T
  // Probe on R
  // Probe on IR[14:12]
  or or_3 (PC_INC, and_10_out, and_11_out, and_12_out, and_13_out, and_14_out, and_15_out, and_16_out, and_17_out, and_18_out);
  and and_19 (and_19_out, D4, T4);
  and and_20 (and_20_out, D5, T5);
  and and_21 (and_21_out, D6, T6);
  or or_4 (or_4_out, D0, D1, D2);
  and and_22 (and_22_out, or_4_out, T5);
  and and_23 (and_23_out, R_prime, T2);
  and and_24 (and_24_out, R_prime, T1);
  or or_5 (or_5_out, D0, D1, D2, D6);
  and and_25 (and_25_out, D1, T5);
  and and_26 (and_26_out, r_t, B[7]);
  and and_27 (and_27_out, r_t, B[6]);
  and and_28 (and_28_out, r_t, B[10]);
  and and_29 (and_29_out, r_t, B[8]);
  and and_30 (OUTR_LD, p, B[10]);
  and and_31 (and_31_out, R, T1);
  and and_32 (and_32_out, D3, T4);
  and and_33 (and_33_out, D5, T4);
  and and_34 (DR_INC, D6, T5);
  and and_35 (and_35_out, D0, T4);
  and and_36 (and_36_out, D1, T4);
  and and_37 (and_37_out, D2, T4);
  and and_38 (and_38_out, D6, T4);
  and and_39 (and_39_out, p, B[10]);
  and and_40 (and_40_out, D3, T4);
  not not_5 (not_5_out, D7);
  and and_41 (and_41_out, T4, or_5_out);
  not not_6 (not_6_out, I);
  or or_6 (or_6_out, and_19_out, and_20_out);
  and and_42 (and_42_out, D5, T4);
  or or_7 (or_7_out, and_21_out, and_22_out);
  and and_43 (and_43_out, R, T1);
  and and_44 (and_44_out, not_5_out, I, T3);
  and and_45 (r_t, D7, not_6_out, T3);
  and and_46 (p, D7, I, T3);
  or or_8 (E_LD, and_25_out, and_26_out, and_27_out, and_28_out, and_29_out);
  or or_9 (RAM_LD, and_31_out, and_32_out, and_33_out);
  or or_10 (DR_LD, and_35_out, and_36_out, and_37_out, and_38_out);
  or or_11 (or_11_out, and_42_out, T0);
  or or_12 (or_12_out, and_39_out, and_40_out);
  or or_13 (or_13_out, and_24_out, and_44_out, and_41_out);
  ENC3BIT enc3bit_1 (
    .out_9(BUS_SELECT), .I1(or_6_out), .I2(or_11_out), .I3(or_7_out), .I4(or_12_out), .I5(and_23_out),
    .I6(and_43_out), .I7(or_13_out));  // open: I0
  and and_47 (and_47_out, r_t, B[10]);
  and and_48 (and_48_out, r_t, B[8]);
  and and_49 (and_49_out, r_t, B[7]);
  and and_50 (and_50_out, r_t, B[6]);
  and and_51 (and_51_out, D1, T5);
  and and_52 (TR_LD, R, T0);
  and and_53 (IR_LD, R_prime, T1);
  assign E_SELECT = and_47_out ? 3'b000 : 3'bz;  // Controlled_Buffer controlled_buffer_2
  assign E_SELECT = and_48_out ? 3'b001 : 3'bz;  // Controlled_Buffer controlled_buffer_3
  assign E_SELECT = and_49_out ? 3'b010 : 3'bz;  // Controlled_Buffer controlled_buffer_4
  assign E_SELECT = and_50_out ? 3'b011 : 3'bz;  // Controlled_Buffer controlled_buffer_5
  assign E_SELECT = and_51_out ? 3'b100 : 3'bz;  // Controlled_Buffer controlled_buffer_6
  and and_54 (and_54_out, D0, T5);
  and and_55 (and_55_out, D1, T5);
  and and_56 (and_56_out, D2, T5);
  and and_57 (and_57_out, r_t, B[9]);
  and and_58 (and_58_out, r_t, B[7]);
  and and_59 (and_59_out, r_t, B[6]);
  and and_60 (and_60_out, p, B[11]);
  and and_61 (AC_INC, r_t, B[5]);
  and and_62 (AC_CLR, r_t, B[11]);
  and and_63 (and_63_out, R_prime, T2);
  D_Flip_Flop u_I (.clk(CLOCK), .D(IR[15]), .Q(I), .en(and_63_out));  // open: Qn, preset, reset
  or or_14 (AC_LD, and_54_out, and_55_out, and_56_out, and_57_out, and_58_out, and_59_out, and_60_out);
  Decoder #(.select(3), .disabled(0), .enable("false")) decoder_1 (
    .out0(D0), .out1(D1), .out2(D2), .out3(D3), .out4(D4), .out5(D5), .out6(D6), .out7(D7), .sel(IR[14:12]));
  and and_64 (and_64_out, R, T2);
  and and_65 (and_65_out, D0, T5);
  and and_66 (and_66_out, D1, T5);
  and and_67 (and_67_out, D2, T5);
  and and_68 (and_68_out, D3, T4);
  and and_69 (and_69_out, D4, T4);
  and and_70 (and_70_out, D5, T5);
  and and_71 (and_71_out, D6, T6);
  and and_72 (and_72_out, D1, T5);
  and and_73 (and_73_out, r_t, B[9]);
  and and_74 (and_74_out, D2, T5);
  and and_75 (and_75_out, p, B[11]);
  and and_76 (and_76_out, r_t, B[11]);
  and and_77 (and_77_out, r_t, B[5]);
  and and_78 (and_78_out, D0, T5);
  and and_79 (and_79_out, r_t, B[6]);
  and and_80 (and_80_out, r_t, B[7]);
  not not_7 (not_7_out, SC_CLR);
  not not_8 (not_8_out, CLOCK);
  assign {ALU_SELECT, ALU_CIN} = and_72_out ? {5{1'b0}} : 5'bz;  // Controlled_Buffer controlled_buffer_7
  assign {ALU_SELECT, ALU_CIN} = and_73_out ? 5'b00010 : 5'bz;  // Controlled_Buffer controlled_buffer_8
  assign {ALU_SELECT, ALU_CIN} = or_15_out ? 5'b00100 : 5'bz;  // Controlled_Buffer controlled_buffer_9
  or or_15 (or_15_out, and_74_out, and_75_out, and_76_out);
  assign {ALU_SELECT, ALU_CIN} = and_77_out ? 5'b00101 : 5'bz;  // Controlled_Buffer controlled_buffer_10
  assign {ALU_SELECT, ALU_CIN} = and_78_out ? 5'b01000 : 5'bz;  // Controlled_Buffer controlled_buffer_11
  assign {ALU_SELECT, ALU_CIN} = and_79_out ? 5'b10000 : 5'bz;  // Controlled_Buffer controlled_buffer_12
  assign {ALU_SELECT, ALU_CIN} = and_80_out ? 5'b11000 : 5'bz;  // Controlled_Buffer controlled_buffer_13
  Counter #(.width(4), .max('hf)) SC (
    .load(SC_CLR), .D(4'b0000), .count(not_7_out), .Q(T), .clk(not_8_out));  // open: carry, clr
  Decoder #(.select(4), .enable("false")) decoder_2 (
    .out0(T0), .out1(T1), .out2(T2), .out3(T3), .out4(T4), .out5(T5), .out6(T6), .out7(T7), .out8(T8),
    .out9(T9), .out10(T10), .out11(T11), .out12(T12), .out13(T13), .out14(T14), .out15(T15), .sel(T));
  or or_16 (SC_CLR, and_64_out, and_65_out, and_66_out, and_67_out, and_68_out, and_69_out, and_70_out, and_71_out, r_t, p);
  REG8BIT u_INPR (.Q(INPR));  // open: D, CLK, CLR, LD, INC
  D_Flip_Flop u_E (.D(EIN), .Q(E), .en(E_LD));  // open: clk, Qn, preset, reset
  // Probe on ALU_X
  and and_81 (and_81_out, p, B[7]);
  and and_82 (and_82_out, p, B[6]);
  and and_83 (and_83_out, p, B[11]);
  and and_84 (and_84_out, p, B[10]);
  and and_85 (and_85_out, D1, T5);
  and and_86 (and_86_out, D0, T5);
  and and_87 (and_87_out, r_t, B[7]);
  and and_88 (and_88_out, r_t, B[6]);
  and and_89 (and_89_out, r_t, B[5]);
  and and_90 (and_90_out, r_t, B[11]);
  and and_91 (and_91_out, r_t, B[9]);
  and and_92 (and_92_out, D2, T5);
  and and_93 (and_93_out, p, B[11]);
  or or_17 (or_17_out, and_81_out, and_82_out);
  or or_18 (or_18_out, and_85_out, and_86_out, and_87_out, and_88_out, and_89_out);
  or or_19 (or_19_out, and_90_out, and_91_out);
  // Probe on ALU_Y
  D_Flip_Flop IEN (.clk(CLOCK), .D(or_17_out), .Q(IEN_q));  // open: Qn, preset, en, reset
  D_Flip_Flop u_FGI (.clk(CLOCK), .Q(FGI), .preset(and_83_out), .en(and_83_out));  // open: D, Qn, reset
  D_Flip_Flop u_FGO (.clk(CLOCK), .Q(FGO), .en(and_84_out));  // open: D, Qn, preset, reset
  assign bit_extender_1_out = {{8{1'b0}}, INPR};  // Bit_Extender bit_extender_1
  not not_9 (not_9_out, E);
  not not_10 (not_10_out, T0);
  not not_11 (not_11_out, T2);
  Multiplexer #(.select(2), .width(16), .enable("false")) multiplexer_2 (
    .in0(AC), .in1({16{1'b0}}), .in2(DR), .in3(bit_extender_1_out), .out(ALU_Y), .sel(enc2bit_1_out_5));
  ENC2BIT enc2bit_1 (.out_5(enc2bit_1_out_5), .I0(or_18_out), .I1(or_19_out), .I2(and_92_out), .I3(and_93_out));
  Multiplexer #(.select(3), .enable("false")) multiplexer_3 (
    .in0(1'b0), .in1(not_9_out), .in2(ALU_Y[0]), .in3(ALU_Y[15]), .in4(alu1bit_16_cout),
    .in5(alu1bit_16_cout), .in6(alu1bit_16_cout), .in7(alu1bit_16_cout), .out(EIN), .sel(E_SELECT));
  not not_12 (not_12_out, T1);
  or or_20 (or_20_out, FGI, FGO);
  and and_94 (and_94_out, IEN_q, not_10_out, not_12_out, not_11_out, or_20_out);
  and and_95 (and_95_out, r_t, B[9]);
  and and_96 (and_96_out, D0, T5);
  and and_97 (and_97_out, D1, T5);
  or or_21 (or_21_out, and_98_out, and_94_out);
  or or_22 (or_22_out, and_96_out, and_97_out);
  ALU1Bit alu1bit_1 (
    .Cin(ALU_CIN), .Ai(ALU_Y[0]), .Bi(ALU_X[0]), .S3S2S1S0(ALU_SELECT), .Ai_1(E), .Ai_1_2(ALU_Y[1]),
    .out_7(AC_IN[0]), .Cout(alu1bit_1_cout));
  ALU1Bit alu1bit_2 (
    .Cin(alu1bit_1_cout), .Ai(ALU_Y[1]), .Bi(ALU_X[1]), .S3S2S1S0(ALU_SELECT), .Ai_1(ALU_Y[0]),
    .Ai_1_2(ALU_Y[1]), .out_7(AC_IN[1]), .Cout(alu1bit_2_cout));
  ALU1Bit alu1bit_3 (
    .Cin(alu1bit_2_cout), .Ai(ALU_Y[2]), .Bi(ALU_X[2]), .S3S2S1S0(ALU_SELECT), .Ai_1(ALU_Y[1]),
    .Ai_1_2(ALU_Y[2]), .out_7(AC_IN[2]), .Cout(alu1bit_3_cout));
  ALU1Bit alu1bit_4 (
    .Cin(alu1bit_3_cout), .Ai(ALU_Y[3]), .Bi(ALU_X[3]), .S3S2S1S0(ALU_SELECT), .Ai_1(ALU_Y[2]),
    .Ai_1_2(ALU_Y[3]), .out_7(AC_IN[3]), .Cout(alu1bit_4_cout));
  ALU1Bit alu1bit_5 (
    .Cin(alu1bit_4_cout), .Ai(ALU_Y[4]), .Bi(ALU_X[4]), .S3S2S1S0(ALU_SELECT), .Ai_1(ALU_Y[3]),
    .Ai_1_2(ALU_Y[4]), .out_7(AC_IN[4]), .Cout(alu1bit_5_cout));
  ALU1Bit alu1bit_6 (
    .Cin(alu1bit_5_cout), .Ai(ALU_Y[5]), .Bi(ALU_X[5]), .S3S2S1S0(ALU_SELECT), .Ai_1(ALU_Y[4]),
    .Ai_1_2(ALU_Y[5]), .out_7(AC_IN[5]), .Cout(alu1bit_6_cout));
  ALU1Bit alu1bit_7 (
    .Cin(alu1bit_6_cout), .Ai(ALU_Y[6]), .Bi(ALU_X[6]), .S3S2S1S0(ALU_SELECT), .Ai_1(ALU_Y[5]),
    .Ai_1_2(ALU_Y[6]), .out_7(AC_IN[6]), .Cout(alu1bit_7_cout));
  ALU1Bit alu1bit_8 (
    .Cin(alu1bit_7_cout), .Ai(ALU_Y[7]), .Bi(ALU_X[7]), .S3S2S1S0(ALU_SELECT), .Ai_1(ALU_Y[6]),
    .Ai_1_2(ALU_Y[7]), .out_7(AC_IN[7]), .Cout(alu1bit_8_cout));
  ALU1Bit alu1bit_9 (
    .Cin(alu1bit_8_cout), .Ai(ALU_Y[8]), .Bi(ALU_X[8]), .S3S2S1S0(ALU_SELECT), .Ai_1(ALU_Y[7]),
    .Ai_1_2(ALU_Y[8]), .out_7(AC_IN[8]), .Cout(alu1bit_9_cout));
  ALU1Bit alu1bit_10 (
    .Cin(alu1bit_9_cout), .Ai(ALU_Y[9]), .Bi(ALU_X[9]), .S3S2S1S0(ALU_SELECT), .Ai_1(ALU_Y[8]),
    .Ai_1_2(ALU_Y[9]), .out_7(AC_IN[9]), .Cout(alu1bit_10_cout));
  ALU1Bit alu1bit_11 (
    .Cin(alu1bit_10_cout), .Ai(ALU_Y[10]), .Bi(ALU_X[10]), .S3S2S1S0(ALU_SELECT), .Ai_1(ALU_Y[9]),
    .Ai_1_2(ALU_Y[10]), .out_7(AC_IN[10]), .Cout(alu1bit_11_cout));
  ALU1Bit alu1bit_12 (
    .Cin(alu1bit_11_cout), .Ai(ALU_Y[11]), .Bi(ALU_X[11]), .S3S2S1S0(ALU_SELECT), .Ai_1(ALU_Y[10]),
    .Ai_1_2(ALU_Y[11]), .out_7(AC_IN[11]), .Cout(alu1bit_12_cout));
  ALU1Bit alu1bit_13 (
    .Cin(alu1bit_12_cout), .Ai(ALU_Y[12]), .Bi(ALU_X[12]), .S3S2S1S0(ALU_SELECT), .Ai_1(ALU_Y[11]),
    .Ai_1_2(ALU_Y[12]), .out_7(AC_IN[12]), .Cout(alu1bit_13_cout));
  ALU1Bit alu1bit_14 (
    .Cin(alu1bit_13_cout), .Ai(ALU_Y[13]), .Bi(ALU_X[13]), .S3S2S1S0(ALU_SELECT), .Ai_1(ALU_Y[12]),
    .Ai_1_2(ALU_Y[13]), .out_7(AC_IN[13]), .Cout(alu1bit_14_cout));
  ALU1Bit alu1bit_15 (
    .Cin(alu1bit_14_cout), .Ai(ALU_Y[14]), .Bi(ALU_X[14]), .S3S2S1S0(ALU_SELECT), .Ai_1(ALU_Y[13]),
    .Ai_1_2(ALU_Y[14]), .out_7(AC_IN[14]), .Cout(alu1bit_15_cout));
  ALU1Bit alu1bit_16 (
    .Cin(alu1bit_15_cout), .Ai(ALU_Y[15]), .Bi(ALU_X[15]), .S3S2S1S0(ALU_SELECT), .Ai_1(ALU_Y[14]),
    .Ai_1_2(E), .out_7(AC_IN[15]), .Cout(alu1bit_16_cout));
  D_Flip_Flop u_R (.clk(CLOCK), .D(or_21_out), .Q(R));  // open: Qn, preset, en, reset
  and and_98 (and_98_out, R, not_13_out);
  ENC1BIT enc1bit_1 (.I0(and_95_out), .I1(or_22_out), .out_3(enc1bit_1_out_3));
  not not_13 (not_13_out, T2);
  Multiplexer #(.width(16), .enable("false")) multiplexer_4 (.in0(AC), .in1(DR), .out(ALU_X), .sel(enc1bit_1_out_3));
  not not_14 (R_prime, R);

  // Other names for the same wires on the sheet: IR[11:0] = B; Opcode[2:0] = IR[14:12]

  // Notes on the sheet:
  //   BUS SYSTEM
  //   CIRCUIT DEBUGGER
  //   PC CONTROL
  //   AR CONTROL
  //   E CONTROL
  //   OUTR CONTROL
  //   RAM CONTROL
  //   DR CONTROL
  //   BUS SELECT
  //   IR CONTROL
  //   E SELECT
  //   TR CONTROL
  //   AC CONTROL
  //   INSTRUCTION FORMAT
  //   BASIC COMPUTER DESIGN
  //   SC CONTROL
  //   AC FUNCTION SELECT
  //   Made by JOEL SAM and KESHAV GOYAL
  //   SEQUENCE TIMING
  //   AC INPUT SELECT
  //   16 BIT ALU
  //   INTERRUPT CYCLE
endmodule

module ALU1Bit (
  input  Cin,
  input  Ai_1,
  input  Ai,
  input  Bi,
  input  [3:0] S3S2S1S0,
  input  Ai_1_2,
  output out_7,
  output Cout
);

  wire adder_1_out, and_1_out, multiplexer_1_out, multiplexer_2_out, not_1_out, not_2_out, not_3_out,
       or_1_out, xor_1_out;

  not not_1 (not_1_out, 1'b0);
  and and_1 (and_1_out, Ai, Bi);
  or or_1 (or_1_out, Ai, Bi);
  xor xor_1 (xor_1_out, Ai, Bi);
  not not_2 (not_2_out, Ai);
  not not_3 (not_3_out, Bi);
  Multiplexer #(.select(2), .enable("false")) multiplexer_1 (
    .in0(Bi), .in1(not_3_out), .in2(1'b0), .in3(not_1_out), .out(multiplexer_1_out), .sel(S3S2S1S0[1:0]));
  Adder #(.width(1)) adder_1 (.a(Ai), .b(multiplexer_1_out), .out(adder_1_out), .cin(Cin), .cout(Cout));
  Multiplexer #(.select(2), .enable("false")) multiplexer_2 (
    .in0(and_1_out), .in1(or_1_out), .in2(xor_1_out), .in3(not_2_out), .out(multiplexer_2_out),
    .sel(S3S2S1S0[1:0]));
  Multiplexer #(.select(2), .enable("false")) multiplexer_3 (
    .in0(adder_1_out), .in1(multiplexer_2_out), .in2(Ai_1), .in3(Ai_1_2), .out(out_7), .sel(S3S2S1S0[3:2]));

  // Notes on the sheet:
  //   Di
endmodule

module ALU (
  input  [15:0] B,
  input  [15:0] A,
  input  [4:0] F3F2F1F0CIN,
  input  EIN,
  output EOUT,
  output [15:0] S
);

  wire adder_1_cout, adder_1_out, adder_2_cout, adder_2_out, adder_3_cout, adder_3_out, adder_4_cout,
       adder_4_out, adder_5_cout, adder_5_out, adder_6_cout, adder_6_out, adder_7_cout, adder_7_out,
       adder_8_cout, adder_8_out, adder_9_cout, adder_9_out, adder_10_cout, adder_10_out, adder_11_cout,
       adder_11_out, adder_12_cout, adder_12_out, adder_13_cout, adder_13_out, adder_14_cout, adder_14_out,
       adder_15_cout, adder_15_out, adder_16_cout, adder_16_out, and_1_out, and_2_out, and_3_out, and_4_out,
       and_5_out, and_6_out, and_7_out, and_8_out, and_9_out, and_10_out, and_11_out, and_12_out, and_13_out,
       and_14_out, and_15_out, and_16_out, multiplexer_1_out, multiplexer_2_out, multiplexer_3_out,
       multiplexer_4_out, multiplexer_5_out, multiplexer_6_out, multiplexer_7_out, multiplexer_8_out,
       multiplexer_9_out, multiplexer_10_out, multiplexer_11_out, multiplexer_12_out, multiplexer_13_out,
       multiplexer_14_out, multiplexer_15_out, multiplexer_16_out, multiplexer_17_out, multiplexer_18_out,
       multiplexer_19_out, multiplexer_20_out, multiplexer_21_out, multiplexer_22_out, multiplexer_23_out,
       multiplexer_24_out, multiplexer_25_out, multiplexer_26_out, multiplexer_27_out, multiplexer_28_out,
       multiplexer_29_out, multiplexer_30_out, multiplexer_31_out, multiplexer_32_out, not_1_out, not_2_out,
       not_3_out, not_4_out, not_5_out, not_6_out, not_7_out, not_8_out, not_9_out, not_10_out, not_11_out,
       not_12_out, not_13_out, not_14_out, not_15_out, not_16_out, not_17_out, not_18_out, not_19_out,
       not_20_out, not_21_out, not_22_out, not_23_out, not_24_out, not_25_out, not_26_out, not_27_out,
       not_28_out, not_29_out, not_30_out, not_31_out, not_32_out, not_33_out, not_34_out, not_35_out,
       not_36_out, not_37_out, not_38_out, not_39_out, not_40_out, not_41_out, not_42_out, not_43_out,
       not_44_out, not_45_out, not_46_out, not_47_out, not_48_out, or_1_out, or_2_out, or_3_out, or_4_out,
       or_5_out, or_6_out, or_7_out, or_8_out, or_9_out, or_10_out, or_11_out, or_12_out, or_13_out,
       or_14_out, or_15_out, or_16_out, xor_1_out, xor_2_out, xor_3_out, xor_4_out, xor_5_out, xor_6_out,
       xor_7_out, xor_8_out, xor_9_out, xor_10_out, xor_11_out, xor_12_out, xor_13_out, xor_14_out,
       xor_15_out, xor_16_out;

  // Probe on B
  // Probe on A
  not not_1 (not_1_out, 1'b0);
  not not_2 (not_2_out, A[0]);
  not not_3 (not_3_out, 1'b0);
  not not_4 (not_4_out, A[1]);
  not not_5 (not_5_out, 1'b0);
  not not_6 (not_6_out, A[2]);
  not not_7 (not_7_out, 1'b0);
  not not_8 (not_8_out, A[3]);
  not not_9 (not_9_out, 1'b0);
  not not_10 (not_10_out, A[4]);
  not not_11 (not_11_out, 1'b0);
  not not_12 (not_12_out, A[5]);
  not not_13 (not_13_out, 1'b0);
  not not_14 (not_14_out, A[6]);
  not not_15 (not_15_out, 1'b0);
  not not_16 (not_16_out, A[7]);
  not not_17 (not_17_out, B[0]);
  and and_1 (and_1_out, A[0], B[0]);
  or or_1 (or_1_out, A[0], B[0]);
  xor xor_1 (xor_1_out, A[0], B[0]);
  not not_18 (not_18_out, B[1]);
  and and_2 (and_2_out, A[1], B[1]);
  or or_2 (or_2_out, A[1], B[1]);
  xor xor_2 (xor_2_out, A[1], B[1]);
  not not_19 (not_19_out, B[2]);
  and and_3 (and_3_out, A[2], B[2]);
  or or_3 (or_3_out, A[2], B[2]);
  xor xor_3 (xor_3_out, A[2], B[2]);
  not not_20 (not_20_out, B[3]);
  and and_4 (and_4_out, A[3], B[3]);
  or or_4 (or_4_out, A[3], B[3]);
  xor xor_4 (xor_4_out, A[3], B[3]);
  not not_21 (not_21_out, B[4]);
  and and_5 (and_5_out, A[4], B[4]);
  or or_5 (or_5_out, A[4], B[4]);
  xor xor_5 (xor_5_out, A[4], B[4]);
  not not_22 (not_22_out, B[5]);
  and and_6 (and_6_out, A[5], B[5]);
  or or_6 (or_6_out, A[5], B[5]);
  xor xor_6 (xor_6_out, A[5], B[5]);
  not not_23 (not_23_out, B[6]);
  and and_7 (and_7_out, A[6], B[6]);
  or or_7 (or_7_out, A[6], B[6]);
  xor xor_7 (xor_7_out, A[6], B[6]);
  not not_24 (not_24_out, B[7]);
  and and_8 (and_8_out, A[7], B[7]);
  or or_8 (or_8_out, A[7], B[7]);
  xor xor_8 (xor_8_out, A[7], B[7]);
  not not_25 (not_25_out, B[8]);
  not not_26 (not_26_out, 1'b0);
  and and_9 (and_9_out, A[8], B[8]);
  or or_9 (or_9_out, A[8], B[8]);
  xor xor_9 (xor_9_out, A[8], B[8]);
  not not_27 (not_27_out, A[8]);
  not not_28 (not_28_out, B[9]);
  not not_29 (not_29_out, 1'b0);
  and and_10 (and_10_out, A[9], B[9]);
  or or_10 (or_10_out, A[9], B[9]);
  xor xor_10 (xor_10_out, A[9], B[9]);
  not not_30 (not_30_out, A[9]);
  not not_31 (not_31_out, B[10]);
  not not_32 (not_32_out, 1'b0);
  and and_11 (and_11_out, A[10], B[10]);
  or or_11 (or_11_out, A[10], B[10]);
  xor xor_11 (xor_11_out, A[10], B[10]);
  not not_33 (not_33_out, A[10]);
  not not_34 (not_34_out, B[11]);
  not not_35 (not_35_out, 1'b0);
  and and_12 (and_12_out, A[11], B[11]);
  or or_12 (or_12_out, A[11], B[11]);
  xor xor_12 (xor_12_out, A[11], B[11]);
  not not_36 (not_36_out, A[11]);
  not not_37 (not_37_out, B[12]);
  not not_38 (not_38_out, 1'b0);
  and and_13 (and_13_out, A[12], B[12]);
  or or_13 (or_13_out, A[12], B[12]);
  xor xor_13 (xor_13_out, A[12], B[12]);
  not not_39 (not_39_out, A[12]);
  not not_40 (not_40_out, B[13]);
  not not_41 (not_41_out, 1'b0);
  and and_14 (and_14_out, A[13], B[13]);
  or or_14 (or_14_out, A[13], B[13]);
  xor xor_14 (xor_14_out, A[13], B[13]);
  not not_42 (not_42_out, A[13]);
  not not_43 (not_43_out, B[14]);
  not not_44 (not_44_out, 1'b0);
  and and_15 (and_15_out, A[14], B[14]);
  or or_15 (or_15_out, A[14], B[14]);
  xor xor_15 (xor_15_out, A[14], B[14]);
  not not_45 (not_45_out, A[14]);
  not not_46 (not_46_out, B[15]);
  not not_47 (not_47_out, 1'b0);
  and and_16 (and_16_out, A[15], B[15]);
  or or_16 (or_16_out, A[15], B[15]);
  xor xor_16 (xor_16_out, A[15], B[15]);
  not not_48 (not_48_out, A[15]);
  Multiplexer #(.select(2), .enable("false")) multiplexer_1 (
    .in0(B[0]), .in1(not_17_out), .in2(1'b0), .in3(not_1_out), .out(multiplexer_1_out), .sel(F3F2F1F0CIN[2:1]));
  Multiplexer #(.select(2), .enable("false")) multiplexer_2 (
    .in0(B[1]), .in1(not_18_out), .in2(1'b0), .in3(not_3_out), .out(multiplexer_2_out), .sel(F3F2F1F0CIN[2:1]));
  Multiplexer #(.select(2), .enable("false")) multiplexer_3 (
    .in0(B[2]), .in1(not_19_out), .in2(1'b0), .in3(not_5_out), .out(multiplexer_3_out), .sel(F3F2F1F0CIN[2:1]));
  Multiplexer #(.select(2), .enable("false")) multiplexer_4 (
    .in0(B[3]), .in1(not_20_out), .in2(1'b0), .in3(not_7_out), .out(multiplexer_4_out), .sel(F3F2F1F0CIN[2:1]));
  Multiplexer #(.select(2), .enable("false")) multiplexer_5 (
    .in0(B[4]), .in1(not_21_out), .in2(1'b0), .in3(not_9_out), .out(multiplexer_5_out), .sel(F3F2F1F0CIN[2:1]));
  Multiplexer #(.select(2), .enable("false")) multiplexer_6 (
    .in0(B[5]), .in1(not_22_out), .in2(1'b0), .in3(not_11_out), .out(multiplexer_6_out),
    .sel(F3F2F1F0CIN[2:1]));
  Multiplexer #(.select(2), .enable("false")) multiplexer_7 (
    .in0(B[6]), .in1(not_23_out), .in2(1'b0), .in3(not_13_out), .out(multiplexer_7_out),
    .sel(F3F2F1F0CIN[2:1]));
  Multiplexer #(.select(2), .enable("false")) multiplexer_8 (
    .in0(B[7]), .in1(not_24_out), .in2(1'b0), .in3(not_15_out), .out(multiplexer_8_out),
    .sel(F3F2F1F0CIN[2:1]));
  Multiplexer #(.select(2), .enable("false")) multiplexer_9 (
    .in0(B[8]), .in1(not_25_out), .in2(1'b0), .in3(not_26_out), .out(multiplexer_9_out),
    .sel(F3F2F1F0CIN[2:1]));
  Multiplexer #(.select(2), .enable("false")) multiplexer_10 (
    .in0(B[9]), .in1(not_28_out), .in2(1'b0), .in3(not_29_out), .out(multiplexer_10_out),
    .sel(F3F2F1F0CIN[2:1]));
  Multiplexer #(.select(2), .enable("false")) multiplexer_11 (
    .in0(B[10]), .in1(not_31_out), .in2(1'b0), .in3(not_32_out), .out(multiplexer_11_out),
    .sel(F3F2F1F0CIN[2:1]));
  Multiplexer #(.select(2), .enable("false")) multiplexer_12 (
    .in0(B[11]), .in1(not_34_out), .in2(1'b0), .in3(not_35_out), .out(multiplexer_12_out),
    .sel(F3F2F1F0CIN[2:1]));
  Multiplexer #(.select(2), .enable("false")) multiplexer_13 (
    .in0(B[12]), .in1(not_37_out), .in2(1'b0), .in3(not_38_out), .out(multiplexer_13_out),
    .sel(F3F2F1F0CIN[2:1]));
  Multiplexer #(.select(2), .enable("false")) multiplexer_14 (
    .in0(B[13]), .in1(not_40_out), .in2(1'b0), .in3(not_41_out), .out(multiplexer_14_out),
    .sel(F3F2F1F0CIN[2:1]));
  Multiplexer #(.select(2), .enable("false")) multiplexer_15 (
    .in0(B[14]), .in1(not_43_out), .in2(1'b0), .in3(not_44_out), .out(multiplexer_15_out),
    .sel(F3F2F1F0CIN[2:1]));
  Multiplexer #(.select(2), .enable("false")) multiplexer_16 (
    .in0(B[15]), .in1(not_46_out), .in2(1'b0), .in3(not_47_out), .out(multiplexer_16_out),
    .sel(F3F2F1F0CIN[2:1]));
  Multiplexer #(.select(2), .enable("false")) multiplexer_17 (
    .in0(and_1_out), .in1(or_1_out), .in2(xor_1_out), .in3(not_2_out), .out(multiplexer_17_out),
    .sel(F3F2F1F0CIN[2:1]));
  Multiplexer #(.select(2), .enable("false")) multiplexer_18 (
    .in0(and_2_out), .in1(or_2_out), .in2(xor_2_out), .in3(not_4_out), .out(multiplexer_18_out),
    .sel(F3F2F1F0CIN[2:1]));
  Multiplexer #(.select(2), .enable("false")) multiplexer_19 (
    .in0(and_3_out), .in1(or_3_out), .in2(xor_3_out), .in3(not_6_out), .out(multiplexer_19_out),
    .sel(F3F2F1F0CIN[2:1]));
  Multiplexer #(.select(2), .enable("false")) multiplexer_20 (
    .in0(and_4_out), .in1(or_4_out), .in2(xor_4_out), .in3(not_8_out), .out(multiplexer_20_out),
    .sel(F3F2F1F0CIN[2:1]));
  Multiplexer #(.select(2), .enable("false")) multiplexer_21 (
    .in0(and_5_out), .in1(or_5_out), .in2(xor_5_out), .in3(not_10_out), .out(multiplexer_21_out),
    .sel(F3F2F1F0CIN[2:1]));
  Multiplexer #(.select(2), .enable("false")) multiplexer_22 (
    .in0(and_6_out), .in1(or_6_out), .in2(xor_6_out), .in3(not_12_out), .out(multiplexer_22_out),
    .sel(F3F2F1F0CIN[2:1]));
  Multiplexer #(.select(2), .enable("false")) multiplexer_23 (
    .in0(and_7_out), .in1(or_7_out), .in2(xor_7_out), .in3(not_14_out), .out(multiplexer_23_out),
    .sel(F3F2F1F0CIN[2:1]));
  Multiplexer #(.select(2), .enable("false")) multiplexer_24 (
    .in0(and_8_out), .in1(or_8_out), .in2(xor_8_out), .in3(not_16_out), .out(multiplexer_24_out),
    .sel(F3F2F1F0CIN[2:1]));
  Multiplexer #(.select(2), .enable("false")) multiplexer_25 (
    .in0(and_9_out), .in1(or_9_out), .in2(xor_9_out), .in3(not_27_out), .out(multiplexer_25_out),
    .sel(F3F2F1F0CIN[2:1]));
  Multiplexer #(.select(2), .enable("false")) multiplexer_26 (
    .in0(and_10_out), .in1(or_10_out), .in2(xor_10_out), .in3(not_30_out), .out(multiplexer_26_out),
    .sel(F3F2F1F0CIN[2:1]));
  Multiplexer #(.select(2), .enable("false")) multiplexer_27 (
    .in0(and_11_out), .in1(or_11_out), .in2(xor_11_out), .in3(not_33_out), .out(multiplexer_27_out),
    .sel(F3F2F1F0CIN[2:1]));
  Multiplexer #(.select(2), .enable("false")) multiplexer_28 (
    .in0(and_12_out), .in1(or_12_out), .in2(xor_12_out), .in3(not_36_out), .out(multiplexer_28_out),
    .sel(F3F2F1F0CIN[2:1]));
  Multiplexer #(.select(2), .enable("false")) multiplexer_29 (
    .in0(and_13_out), .in1(or_13_out), .in2(xor_13_out), .in3(not_39_out), .out(multiplexer_29_out),
    .sel(F3F2F1F0CIN[2:1]));
  Multiplexer #(.select(2), .enable("false")) multiplexer_30 (
    .in0(and_14_out), .in1(or_14_out), .in2(xor_14_out), .in3(not_42_out), .out(multiplexer_30_out),
    .sel(F3F2F1F0CIN[2:1]));
  Multiplexer #(.select(2), .enable("false")) multiplexer_31 (
    .in0(and_15_out), .in1(or_15_out), .in2(xor_15_out), .in3(not_45_out), .out(multiplexer_31_out),
    .sel(F3F2F1F0CIN[2:1]));
  Multiplexer #(.select(2), .enable("false")) multiplexer_32 (
    .in0(and_16_out), .in1(or_16_out), .in2(xor_16_out), .in3(not_48_out), .out(multiplexer_32_out),
    .sel(F3F2F1F0CIN[2:1]));
  Adder #(.width(1)) adder_1 (
    .a(A[0]), .b(multiplexer_1_out), .out(adder_1_out), .cin(F3F2F1F0CIN[0]), .cout(adder_1_cout));
  Adder #(.width(1)) adder_2 (
    .a(A[1]), .b(multiplexer_2_out), .out(adder_2_out), .cin(adder_1_cout), .cout(adder_2_cout));
  Adder #(.width(1)) adder_3 (
    .a(A[2]), .b(multiplexer_3_out), .out(adder_3_out), .cin(adder_2_cout), .cout(adder_3_cout));
  Adder #(.width(1)) adder_4 (
    .a(A[3]), .b(multiplexer_4_out), .out(adder_4_out), .cin(adder_3_cout), .cout(adder_4_cout));
  Adder #(.width(1)) adder_5 (
    .a(A[4]), .b(multiplexer_5_out), .out(adder_5_out), .cin(adder_4_cout), .cout(adder_5_cout));
  Adder #(.width(1)) adder_6 (
    .a(A[5]), .b(multiplexer_6_out), .out(adder_6_out), .cin(adder_5_cout), .cout(adder_6_cout));
  Adder #(.width(1)) adder_7 (
    .a(A[6]), .b(multiplexer_7_out), .out(adder_7_out), .cin(adder_6_cout), .cout(adder_7_cout));
  Adder #(.width(1)) adder_8 (
    .a(A[7]), .b(multiplexer_8_out), .out(adder_8_out), .cin(adder_7_cout), .cout(adder_8_cout));
  Adder #(.width(1)) adder_9 (
    .a(A[8]), .b(multiplexer_9_out), .out(adder_9_out), .cin(adder_8_cout), .cout(adder_9_cout));
  Adder #(.width(1)) adder_10 (
    .a(A[9]), .b(multiplexer_10_out), .out(adder_10_out), .cin(adder_9_cout), .cout(adder_10_cout));
  Adder #(.width(1)) adder_11 (
    .a(A[10]), .b(multiplexer_11_out), .out(adder_11_out), .cin(adder_10_cout), .cout(adder_11_cout));
  Adder #(.width(1)) adder_12 (
    .a(A[11]), .b(multiplexer_12_out), .out(adder_12_out), .cin(adder_11_cout), .cout(adder_12_cout));
  Adder #(.width(1)) adder_13 (
    .a(A[12]), .b(multiplexer_13_out), .out(adder_13_out), .cin(adder_12_cout), .cout(adder_13_cout));
  Adder #(.width(1)) adder_14 (
    .a(A[13]), .b(multiplexer_14_out), .out(adder_14_out), .cin(adder_13_cout), .cout(adder_14_cout));
  Adder #(.width(1)) adder_15 (
    .a(A[14]), .b(multiplexer_15_out), .out(adder_15_out), .cin(adder_14_cout), .cout(adder_15_cout));
  Adder #(.width(1)) adder_16 (
    .a(A[15]), .b(multiplexer_16_out), .out(adder_16_out), .cin(adder_15_cout), .cout(adder_16_cout));
  Multiplexer #(.select(2), .enable("false")) multiplexer_33 (
    .in0(adder_16_cout), .in1(adder_16_cout), .in2(A[15]), .in3(A[0]), .out(EOUT), .sel(F3F2F1F0CIN[4:3]));
  Multiplexer #(.select(2), .enable("false")) multiplexer_34 (
    .in0(adder_1_out), .in1(multiplexer_17_out), .in2(EIN), .in3(A[1]), .out(S[0]), .sel(F3F2F1F0CIN[4:3]));
  Multiplexer #(.select(2), .enable("false")) multiplexer_35 (
    .in0(adder_2_out), .in1(multiplexer_18_out), .in2(A[0]), .in3(A[2]), .out(S[1]), .sel(F3F2F1F0CIN[4:3]));
  Multiplexer #(.select(2), .enable("false")) multiplexer_36 (
    .in0(adder_3_out), .in1(multiplexer_19_out), .in2(A[1]), .in3(A[3]), .out(S[2]), .sel(F3F2F1F0CIN[4:3]));
  Multiplexer #(.select(2), .enable("false")) multiplexer_37 (
    .in0(adder_4_out), .in1(multiplexer_20_out), .in2(A[2]), .in3(A[4]), .out(S[3]), .sel(F3F2F1F0CIN[4:3]));
  Multiplexer #(.select(2), .enable("false")) multiplexer_38 (
    .in0(adder_5_out), .in1(multiplexer_21_out), .in2(A[3]), .in3(A[5]), .out(S[4]), .sel(F3F2F1F0CIN[4:3]));
  Multiplexer #(.select(2), .enable("false")) multiplexer_39 (
    .in0(adder_6_out), .in1(multiplexer_22_out), .in2(A[4]), .in3(A[6]), .out(S[5]), .sel(F3F2F1F0CIN[4:3]));
  Multiplexer #(.select(2), .enable("false")) multiplexer_40 (
    .in0(adder_7_out), .in1(multiplexer_23_out), .in2(A[5]), .in3(A[7]), .out(S[6]), .sel(F3F2F1F0CIN[4:3]));
  Multiplexer #(.select(2), .enable("false")) multiplexer_41 (
    .in0(adder_8_out), .in1(multiplexer_24_out), .in2(A[6]), .in3(A[8]), .out(S[7]), .sel(F3F2F1F0CIN[4:3]));
  Multiplexer #(.select(2), .enable("false")) multiplexer_42 (
    .in0(adder_9_out), .in1(multiplexer_25_out), .in2(A[7]), .in3(A[9]), .out(S[8]), .sel(F3F2F1F0CIN[4:3]));
  Multiplexer #(.select(2), .enable("false")) multiplexer_43 (
    .in0(adder_10_out), .in1(multiplexer_26_out), .in2(A[8]), .in3(A[10]), .out(S[9]), .sel(F3F2F1F0CIN[4:3]));
  Multiplexer #(.select(2), .enable("false")) multiplexer_44 (
    .in0(adder_11_out), .in1(multiplexer_27_out), .in2(A[9]), .in3(A[11]), .out(S[10]), .sel(F3F2F1F0CIN[4:3]));
  Multiplexer #(.select(2), .enable("false")) multiplexer_45 (
    .in0(adder_12_out), .in1(multiplexer_28_out), .in2(A[10]), .in3(A[12]), .out(S[11]),
    .sel(F3F2F1F0CIN[4:3]));
  Multiplexer #(.select(2), .enable("false")) multiplexer_46 (
    .in0(adder_13_out), .in1(multiplexer_29_out), .in2(A[11]), .in3(A[13]), .out(S[12]),
    .sel(F3F2F1F0CIN[4:3]));
  Multiplexer #(.select(2), .enable("false")) multiplexer_47 (
    .in0(adder_14_out), .in1(multiplexer_30_out), .in2(A[12]), .in3(A[14]), .out(S[13]),
    .sel(F3F2F1F0CIN[4:3]));
  Multiplexer #(.select(2), .enable("false")) multiplexer_48 (
    .in0(adder_15_out), .in1(multiplexer_31_out), .in2(A[13]), .in3(A[15]), .out(S[14]),
    .sel(F3F2F1F0CIN[4:3]));
  Multiplexer #(.select(2), .enable("false")) multiplexer_49 (
    .in0(adder_16_out), .in1(multiplexer_32_out), .in2(A[14]), .in3(EIN), .out(S[15]), .sel(F3F2F1F0CIN[4:3]));

  // Notes on the sheet:
  //   Di
  //   Di
  //   Di
  //   Di
  //   Di
  //   Di
  //   Di
  //   Di
  //   Di
  //   Di
  //   Di
  //   Di
  //   Di
  //   Di
  //   Di
  //   Di
endmodule

module REG16BIT (
  input  [15:0] D,
  input  CLK,
  input  CLR,
  input  LD,
  input  INC,
  output [15:0] Q
);

  wire [1:0] enc2bit_1_out_5;
  wire [15:0] adder_1_out, multiplexer_1_out;

  Adder #(.width(16)) adder_1 (.a(Q), .b(16'h1), .out(adder_1_out));  // open: cin, cout
  ENC2BIT enc2bit_1 (.out_5(enc2bit_1_out_5), .I1(CLR), .I2(LD), .I3(INC));  // open: I0
  Multiplexer #(.select(2), .width(16), .enable("false")) multiplexer_1 (
    .in0(Q), .in1({16{1'b0}}), .in2(D), .in3(adder_1_out), .out(multiplexer_1_out), .sel(enc2bit_1_out_5));
  Register #(.width(16)) register_1 (.D(multiplexer_1_out), .Q(Q), .clk(CLK));  // open: en, clr
endmodule

module REG8BIT (
  input  [7:0] D,
  input  CLK,
  input  CLR,
  input  LD,
  input  INC,
  output [7:0] Q
);

  wire [1:0] enc2bit_1_out_5;
  wire [7:0] adder_1_out, multiplexer_1_out;

  Adder adder_1 (.a(Q), .b(8'h1), .out(adder_1_out));  // open: cin, cout
  ENC2BIT enc2bit_1 (.out_5(enc2bit_1_out_5), .I1(CLR), .I2(LD), .I3(INC));  // open: I0
  Multiplexer #(.select(2), .width(8), .enable("false")) multiplexer_1 (
    .in0(Q), .in1({8{1'b0}}), .in2(D), .in3(adder_1_out), .out(multiplexer_1_out), .sel(enc2bit_1_out_5));
  Register register_1 (.D(multiplexer_1_out), .Q(Q), .clk(CLK));  // open: en, clr
endmodule

module REG12BIT (
  input  [11:0] D,
  input  CLK,
  input  CLR,
  input  LD,
  input  INC,
  output [11:0] Q
);

  wire [1:0] enc2bit_1_out_5;
  wire [11:0] adder_1_out, multiplexer_1_out;

  Adder #(.width(12)) adder_1 (.a(Q), .b(12'h1), .out(adder_1_out));  // open: cin, cout
  ENC2BIT enc2bit_1 (.out_5(enc2bit_1_out_5), .I1(CLR), .I2(LD), .I3(INC));  // open: I0
  Multiplexer #(.select(2), .width(12), .enable("false")) multiplexer_1 (
    .in0(Q), .in1({12{1'b0}}), .in2(D), .in3(adder_1_out), .out(multiplexer_1_out), .sel(enc2bit_1_out_5));
  Register #(.width(12)) register_1 (.D(multiplexer_1_out), .Q(Q), .clk(CLK));  // open: en, clr
endmodule

module ENC3BIT (
  input  I0,
  input  I1,
  input  I2,
  input  I3,
  input  I4,
  input  I5,
  input  I6,
  input  I7,
  output [2:0] out_9
);

  wire or_1_out;
  wire [2:0] or_4_out;

  or or_1 (or_1_out, I0, I1, I2, I3, I4, I5, I6, I7);
  or or_2 (or_4_out[2], I7, I6, I5, I4);
  or or_3 (or_4_out[1], I7, I6, I3, I2);
  or or_4 (or_4_out[0], I7, I5, I3, I1);
  assign out_9 = or_1_out ? or_4_out : 3'bz;  // Controlled_Buffer controlled_buffer_1
endmodule

module ENC2BIT (
  input  I0,
  input  I1,
  input  I2,
  input  I3,
  output [1:0] out_5
);

  wire or_1_out;
  wire [1:0] or_2_out;

  or or_1 (or_1_out, I0, I1, I2, I3);
  or or_2 (or_2_out[0], I1, I3);
  or or_3 (or_2_out[1], I2, I3);
  assign out_5 = or_1_out ? or_2_out : 2'bz;  // Controlled_Buffer controlled_buffer_1
endmodule

module ENC1BIT (
  input  I0,
  input  I1,
  output out_3
);

  wire or_1_out;

  assign out_3 = or_1_out ? I1 : 1'bz;  // Controlled_Buffer controlled_buffer_1
  or or_1 (or_1_out, I0, I1);
endmodule

module test (
  input  [15:0] in_1,
  output [15:0] out_2
);

  wire clock_1_out, decoder_1_out4;
  wire [2:0] counter_1_q;

  Clock clock_1 (.out(clock_1_out));
  Counter #(.width(3), .max('h7)) counter_1 (.Q(counter_1_q), .clk(clock_1_out));  // open: load, D, count, carry, clr
  Decoder #(.select(3), .enable("false")) decoder_1 (
    .out4(decoder_1_out4), .sel(counter_1_q));  // open: out0, out1, out2, out3, out5, out6, out7
  REG16BIT reg16bit_1 (.D(in_1), .Q(out_2), .CLK(clock_1_out), .CLR(1'b0), .LD(decoder_1_out4), .INC(1'b0));
endmodule
