// Logisim project 4x4_RAM.circ as structural Verilog: 2 circuits, main circuit Binary Cell
module BC (
  input  Select,
  input  INPUT,
  input  CLOCK,
  input  Read_Write,
  output OUTPUT
);

  wire and_1_out, and_2_out, not_1_out, not_2_out, s_r_ff_1_q;

  not not_1 (not_1_out, INPUT);
  and and_1 (and_1_out, Select, INPUT, not_2_out);
  and and_2 (and_2_out, Select, not_1_out, not_2_out);
  not not_2 (not_2_out, Read_Write);
  S_R_Flip_Flop s_r_ff_1 (.S(and_1_out), .clk(CLOCK), .R(and_2_out), .Q(s_r_ff_1_q));  // open: Qn, preset, reset, en
  and and_3 (OUTPUT, Select, s_r_ff_1_q, Read_Write);
endmodule

module Binary_Cell (
  input  in_1,
  input  in_2,
  input  in_3,
  input  in_4,
  input  in_5,
  input  [1:0] in_6,
  input  in_7,
  output out_8,
  output out_9,
  output out_10,
  output out_11
);

  wire bc_1_output, bc_2_output, bc_3_output, bc_4_output, bc_5_output, bc_6_output, bc_7_output,
       bc_8_output, bc_9_output, bc_10_output, bc_11_output, bc_12_output, bc_13_output, bc_14_output,
       bc_15_output, bc_16_output, clock_1_out, decoder_1_out0, decoder_1_out1, decoder_1_out2,
       decoder_1_out3;

  Decoder #(.select(2)) decoder_1 (
    .out0(decoder_1_out0), .out1(decoder_1_out1), .out2(decoder_1_out2), .out3(decoder_1_out3), .sel(in_6),
    .en(in_5));
  Clock clock_1 (.out(clock_1_out));
  BC bc_1 (.INPUT(in_1), .CLOCK(clock_1_out), .OUTPUT(bc_1_output), .Read_Write(in_7), .Select(decoder_1_out0));
  BC bc_2 (.INPUT(in_1), .CLOCK(clock_1_out), .OUTPUT(bc_2_output), .Read_Write(in_7), .Select(decoder_1_out1));
  BC bc_3 (.INPUT(in_1), .CLOCK(clock_1_out), .OUTPUT(bc_3_output), .Read_Write(in_7), .Select(decoder_1_out2));
  BC bc_4 (.INPUT(in_1), .CLOCK(clock_1_out), .OUTPUT(bc_4_output), .Read_Write(in_7), .Select(decoder_1_out3));
  or or_1 (out_8, bc_4_output, bc_3_output, bc_2_output, bc_1_output);
  BC bc_5 (.INPUT(in_2), .CLOCK(clock_1_out), .OUTPUT(bc_5_output), .Read_Write(in_7), .Select(decoder_1_out0));
  BC bc_6 (.INPUT(in_2), .CLOCK(clock_1_out), .OUTPUT(bc_6_output), .Read_Write(in_7), .Select(decoder_1_out1));
  BC bc_7 (.INPUT(in_2), .CLOCK(clock_1_out), .OUTPUT(bc_7_output), .Read_Write(in_7), .Select(decoder_1_out2));
  BC bc_8 (.INPUT(in_2), .CLOCK(clock_1_out), .OUTPUT(bc_8_output), .Read_Write(in_7), .Select(decoder_1_out3));
  or or_2 (out_10, bc_8_output, bc_7_output, bc_6_output, bc_5_output);
  BC bc_9 (.INPUT(in_3), .CLOCK(clock_1_out), .OUTPUT(bc_9_output), .Read_Write(in_7), .Select(decoder_1_out0));
  BC bc_10 (.INPUT(in_3), .CLOCK(clock_1_out), .OUTPUT(bc_10_output), .Read_Write(in_7), .Select(decoder_1_out1));
  BC bc_11 (.INPUT(in_3), .CLOCK(clock_1_out), .OUTPUT(bc_11_output), .Read_Write(in_7), .Select(decoder_1_out2));
  BC bc_12 (.INPUT(in_3), .CLOCK(clock_1_out), .OUTPUT(bc_12_output), .Read_Write(in_7), .Select(decoder_1_out3));
  or or_3 (out_11, bc_12_output, bc_11_output, bc_10_output, bc_9_output);
  BC bc_13 (.INPUT(in_4), .CLOCK(clock_1_out), .OUTPUT(bc_13_output), .Read_Write(in_7), .Select(decoder_1_out0));
  BC bc_14 (.INPUT(in_4), .CLOCK(clock_1_out), .OUTPUT(bc_14_output), .Read_Write(in_7), .Select(decoder_1_out1));
  BC bc_15 (.INPUT(in_4), .CLOCK(clock_1_out), .OUTPUT(bc_15_output), .Read_Write(in_7), .Select(decoder_1_out2));
  BC bc_16 (.INPUT(in_4), .CLOCK(clock_1_out), .OUTPUT(bc_16_output), .Read_Write(in_7), .Select(decoder_1_out3));
  or or_4 (out_9, bc_15_output, bc_16_output, bc_14_output, bc_13_output);
endmodule
