// Logisim project 2_bit_Multiplier_circuit.circ as structural Verilog: 1 circuit, main circuit main
module main (
  input  A0,
  input  B0,
  input  A1,
  input  B1,
  output C0,
  output C1,
  output C2,
  output C3
);

  wire adder_1_cout, and_2_out, and_3_out, and_4_out;

  and and_1 (C0, A0, B0);
  and and_2 (and_2_out, A1, B0);
  and and_3 (and_3_out, A0, B1);
  and and_4 (and_4_out, A1, B1);
  Adder #(.width(1)) adder_1 (.a(and_3_out), .b(and_2_out), .out(C1), .cout(adder_1_cout));  // open: cin
  Adder #(.width(1)) adder_2 (.a(adder_1_cout), .b(and_4_out), .out(C2), .cout(C3));  // open: cin
endmodule
