// Logisim project 8_bit_Multiplier_circuit.circ as structural Verilog: 1 circuit, main circuit main
module main (
  input  [3:0] A3A2A1A0,
  input  [3:0] B3B2B1B0,
  output [7:0] out_3
);

  wire adder_1_cout, adder_1_out, adder_2_cout, adder_2_out, adder_3_cout, adder_3_out, adder_4_cout,
       adder_4_out, adder_5_cout, adder_5_out, adder_7_cout, adder_8_cout, adder_8_out, adder_9_cout,
       adder_10_cout, adder_11_cout, adder_12_cout, and_2_out, and_3_out, and_4_out, and_5_out, and_6_out,
       and_7_out, and_8_out, and_9_out, and_10_out, and_11_out, and_12_out, and_13_out, and_14_out,
       and_15_out, and_16_out;

  and and_1 (out_3[0], B3B2B1B0[0], A3A2A1A0[0]);
  and and_2 (and_2_out, A3A2A1A0[1], B3B2B1B0[0]);
  and and_3 (and_3_out, A3A2A1A0[0], B3B2B1B0[1]);
  and and_4 (and_4_out, A3A2A1A0[2], B3B2B1B0[0]);
  and and_5 (and_5_out, A3A2A1A0[1], B3B2B1B0[1]);
  and and_6 (and_6_out, A3A2A1A0[0], B3B2B1B0[2]);
  and and_7 (and_7_out, A3A2A1A0[3], B3B2B1B0[0]);
  and and_8 (and_8_out, A3A2A1A0[2], B3B2B1B0[1]);
  and and_9 (and_9_out, A3A2A1A0[1], B3B2B1B0[2]);
  and and_10 (and_10_out, A3A2A1A0[0], B3B2B1B0[3]);
  and and_11 (and_11_out, A3A2A1A0[3], B3B2B1B0[1]);
  and and_12 (and_12_out, A3A2A1A0[2], B3B2B1B0[2]);
  and and_13 (and_13_out, A3A2A1A0[1], B3B2B1B0[3]);
  and and_14 (and_14_out, A3A2A1A0[3], B3B2B1B0[2]);
  and and_15 (and_15_out, A3A2A1A0[1], B3B2B1B0[3]);
  and and_16 (and_16_out, A3A2A1A0[3], B3B2B1B0[3]);
  Adder #(.width(1)) adder_1 (.a(and_4_out), .b(and_5_out), .out(adder_1_out), .cin(adder_7_cout), .cout(adder_1_cout));
  Adder #(.width(1)) adder_2 (.a(and_7_out), .b(and_8_out), .out(adder_2_out), .cin(adder_1_cout), .cout(adder_2_cout));
  Adder #(.width(1)) adder_3 (.a(and_9_out), .b(and_10_out), .out(adder_3_out), .cout(adder_3_cout));  // open: cin
  Adder #(.width(1)) adder_4 (
    .a(and_11_out), .b(and_12_out), .out(adder_4_out), .cin(adder_3_cout), .cout(adder_4_cout));
  Adder #(.width(1)) adder_5 (
    .a(and_14_out), .b(and_15_out), .out(adder_5_out), .cin(adder_4_cout), .cout(adder_5_cout));
  Adder #(.width(1)) adder_6 (.a(adder_5_cout), .b(and_16_out), .out(out_3[6]), .cin(adder_12_cout), .cout(out_3[7]));
  Adder #(.width(1)) adder_7 (.a(and_2_out), .b(and_3_out), .out(out_3[1]), .cout(adder_7_cout));  // open: cin
  Adder #(.width(1)) adder_8 (.a(adder_2_cout), .b(adder_4_out), .out(adder_8_out), .cout(adder_8_cout));  // open: cin
  Adder #(.width(1)) adder_9 (.a(adder_1_out), .b(and_6_out), .out(out_3[2]), .cout(adder_9_cout));  // open: cin
  Adder #(.width(1)) adder_10 (
    .a(adder_2_out), .b(adder_3_out), .out(out_3[3]), .cin(adder_9_cout), .cout(adder_10_cout));
  Adder #(.width(1)) adder_11 (
    .a(adder_8_out), .b(and_13_out), .out(out_3[4]), .cin(adder_10_cout), .cout(adder_11_cout));
  Adder #(.width(1)) adder_12 (
    .a(adder_8_cout), .b(adder_5_out), .out(out_3[5]), .cin(adder_11_cout), .cout(adder_12_cout));
endmodule
