// Logisim project Booth's_Algorithm.circ as structural Verilog: 1 circuit, main circuit main
module main (
  input  [2:0] in_1,
  input  Enable,
  input  [1:0] in_3,
  input  _1,
  input  [1:0] in_5,
  input  in_6,
  input  in_7,
  input  [2:0] in_8,
  input  [1:0] in_9,
  input  Enable_2,
  input  [1:0] in_11,
  input  in_12,
  input  [1:0] in_13,
  input  in_14,
  input  in_15,
  input  [2:0] in_16,
  output [3:0] C3_A3_A2_A1,
  output [4:0] C_A3_A2_A1_A0,
  output [3:0] _000A0,
  output [3:0] A3A2A1A0,
  output Q0,
  output [3:0] A0_0_0_0,
  output [3:0] Q3Q2Q1Q0,
  output [3:0] New_Q,
  output [3:0] _0_Q3_Q2_Q1,
  output [3:0] out_26,
  output [3:0] out_27,
  output [3:0] out_28,
  output [1:0] out_29,
  output [3:0] out_30,
  output [3:0] out_31,
  output [3:0] out_32
);

  wire clock_1_out, clock_2_out, comparator_1_eq, comparator_2_eq, not_1_out, not_2_out, register_7_q;
  wire [1:0] bit_extender_1_out, bit_extender_2_out, shifter_3_out;
  wire [2:0] counter_1_q, counter_2_q;
  wire [3:0] adder_1_out, adder_2_out, controlled_buffer_1_out, controlled_buffer_2_out,
       controlled_buffer_3_out, controlled_buffer_4_out, register_1_q, register_4_q, register_5_q,
       register_6_q, subtractor_1_out;
  wire [4:4] shifter_4_out;

  Clock clock_1 (.out(clock_1_out));
  Register #(.width(4)) register_1 (.en(Enable), .Q(register_1_q), .clk(clock_1_out));  // open: D, clr
  Register #(.width(4)) register_2 (
    .D(controlled_buffer_2_out), .en(Enable), .Q(A3A2A1A0), .clk(clock_1_out));  // open: clr
  Register #(.width(4)) register_3 (
    .D(controlled_buffer_1_out), .en(Enable), .Q(Q3Q2Q1Q0), .clk(clock_1_out));  // open: clr
  Clock clock_2 (.out(clock_2_out));
  Adder #(.width(4)) adder_1 (.a(A3A2A1A0), .b(register_1_q), .out(adder_1_out), .cout(C_A3_A2_A1_A0[4]));  // open: cin
  Shifter #(.width(4), .shift("lr")) shifter_1 (.in(Q3Q2Q1Q0), .\dist (in_5), .out(_0_Q3_Q2_Q1));
  Register #(.width(4)) register_4 (.en(Enable_2), .Q(register_4_q), .clk(clock_2_out));  // open: D, clr
  Register #(.width(4)) register_5 (
    .D(controlled_buffer_4_out), .en(Enable_2), .Q(register_5_q), .clk(clock_2_out));  // open: clr
  Register #(.width(4)) register_6 (
    .D(controlled_buffer_3_out), .en(Enable_2), .Q(register_6_q), .clk(clock_2_out));  // open: clr
  Adder #(.width(4)) adder_2 (.a(register_5_q), .b(register_4_q), .out(adder_2_out));  // open: cin, cout
  Subtractor #(.width(4)) subtractor_1 (.a(register_5_q), .b(register_4_q), .out(subtractor_1_out));  // open: bin, bout
  assign bit_extender_1_out = {{1{1'b0}}, register_6_q[0]};  // Bit_Extender bit_extender_1
  Register #(.width(1)) register_7 (
    .D(register_6_q[0]), .en(Enable_2), .Q(register_7_q), .clk(clock_2_out));  // open: clr
  Shifter #(.width(4), .shift("lr")) shifter_2 (.in(register_6_q), .\dist (in_13), .out(out_32));
  Multiplexer #(.width(4)) multiplexer_1 (
    .in0(A3A2A1A0), .in1(adder_1_out), .out(C_A3_A2_A1_A0[3:0]), .sel(Q0), .en(Enable));
  and and_1 (Q0, Q3Q2Q1Q0[0], _1);
  Counter #(.width(3), .max('h7)) counter_1 (
    .load(in_6), .count(in_7), .Q(counter_1_q), .clk(clock_1_out));  // open: D, carry, clr
  Shifter #(.width(2)) shifter_3 (.in(bit_extender_1_out), .\dist (in_12), .out(shifter_3_out));
  assign bit_extender_2_out = {{1{1'b0}}, register_7_q};  // Bit_Extender bit_extender_2
  Counter #(.width(3), .max('h7)) counter_2 (
    .load(in_14), .count(in_15), .Q(counter_2_q), .clk(clock_2_out));  // open: D, carry, clr
  Comparator #(.width(3)) comparator_1 (.a(counter_1_q), .b(in_8), .eq(comparator_1_eq));  // open: gt, lt
  Adder #(.width(2)) adder_3 (.a(shifter_3_out), .b(bit_extender_2_out), .out(out_29));  // open: cin, cout
  Comparator #(.width(3)) comparator_2 (.a(counter_2_q), .b(in_16), .eq(comparator_2_eq));  // open: gt, lt
  not not_1 (not_1_out, comparator_1_eq);
  assign controlled_buffer_1_out = not_1_out ? New_Q : 4'bz;  // Controlled_Buffer controlled_buffer_1
  assign controlled_buffer_2_out = not_1_out ? C3_A3_A2_A1 : 4'bz;  // Controlled_Buffer controlled_buffer_2
  Multiplexer #(.select(2), .width(4)) multiplexer_2 (
    .in0(register_5_q), .in1(adder_2_out), .in2(subtractor_1_out), .in3(register_5_q), .out(out_26),
    .sel(out_29), .en(Enable_2));
  Adder #(.width(4)) adder_4 (.a(out_30), .b(out_32), .out(out_31));  // open: cin, cout
  not not_2 (not_2_out, comparator_2_eq);
  assign controlled_buffer_3_out = not_2_out ? out_31 : 4'bz;  // Controlled_Buffer controlled_buffer_3
  assign controlled_buffer_4_out = not_2_out ? out_27 : 4'bz;  // Controlled_Buffer controlled_buffer_4
  Shifter #(.width(5), .shift("lr")) shifter_4 (
    .in(C_A3_A2_A1_A0), .\dist (in_1), .out({shifter_4_out[4], C3_A3_A2_A1}));
  assign _000A0 = {{3{1'b0}}, C_A3_A2_A1_A0[0]};  // Bit_Extender bit_extender_3
  assign out_28 = {{3{1'b0}}, out_26[0]};  // Bit_Extender bit_extender_4
  Adder #(.width(4)) adder_5 (.a(A0_0_0_0), .b(_0_Q3_Q2_Q1), .out(New_Q));  // open: cin, cout
  Shifter #(.width(4), .shift("lr")) shifter_5 (.in(out_26), .\dist (in_9), .out(out_27));
  Shifter #(.width(4)) shifter_6 (.in(_000A0), .\dist (in_3), .out(A0_0_0_0));
  Shifter #(.width(4)) shifter_7 (.in(out_28), .\dist (in_11), .out(out_30));

  // Notes on the sheet:
  //   A0 Q3 Q2 Q1
endmodule
