// Logisim project Shift_and_Add_Multiplication_Algorithm .circ as structural Verilog: 1 circuit, main circuit main
module main (
  input  in_1,
  input  [2:0] in_2,
  input  [1:0] in_3,
  input  [1:0] in_4,
  input  in_5,
  input  in_6,
  input  [2:0] in_7,
  output [4:0] C_A3_A2_A1_A0,
  output [3:0] out_9,
  output [3:0] _0_0_0_A0,
  output [3:0] out_11,
  output [3:0] out_12,
  output [3:0] out_13,
  output Q0,
  output [3:0] out_15,
  output [3:0] _0_Q3_Q2_Q1
);

  wire clock_1_out, comparator_1_gt, not_1_out;
  wire [2:0] counter_1_q;
  wire [3:0] adder_1_out, controlled_buffer_1_out, controlled_buffer_2_out, register_1_q;
  wire [4:4] shifter_2_out;

  Clock clock_1 (.out(clock_1_out));
  Register #(.width(4)) register_1 (.en(in_1), .Q(register_1_q), .clk(clock_1_out));  // open: D, clr
  Register #(.width(4)) register_2 (
    .D(controlled_buffer_2_out), .en(in_1), .Q(out_11), .clk(clock_1_out));  // open: clr
  Register #(.width(4)) register_3 (
    .D(controlled_buffer_1_out), .en(in_1), .Q(out_12), .clk(clock_1_out));  // open: clr
  Shifter #(.width(4), .shift("lr")) shifter_1 (.in(out_12), .\dist (in_4), .out(_0_Q3_Q2_Q1));
  Counter #(.width(3), .max('h7)) counter_1 (
    .load(in_5), .count(in_6), .Q(counter_1_q), .clk(clock_1_out));  // open: D, carry, clr
  Adder #(.width(4)) adder_1 (.a(out_11), .b(register_1_q), .out(adder_1_out), .cout(C_A3_A2_A1_A0[4]));  // open: cin
  buf and_1 (Q0, out_12[0]);  // AND_Gate
  Multiplexer #(.width(4)) multiplexer_1 (
    .in0(out_11), .in1(adder_1_out), .out(C_A3_A2_A1_A0[3:0]), .sel(Q0), .en(in_1));
  Comparator #(.width(3)) comparator_1 (.a(counter_1_q), .b(in_7), .gt(comparator_1_gt));  // open: eq, lt
  not not_1 (not_1_out, comparator_1_gt);
  assign controlled_buffer_1_out = not_1_out ? out_15 : 4'bz;  // Controlled_Buffer controlled_buffer_1
  assign controlled_buffer_2_out = not_1_out ? out_9 : 4'bz;  // Controlled_Buffer controlled_buffer_2
  assign _0_0_0_A0 = {{3{1'b0}}, C_A3_A2_A1_A0[0]};  // Bit_Extender bit_extender_1
  Shifter #(.width(5), .shift("lr")) shifter_2 (.in(C_A3_A2_A1_A0), .\dist (in_2), .out({shifter_2_out[4], out_9}));
  Shifter #(.width(4)) shifter_3 (.in(_0_0_0_A0), .\dist (in_3), .out(out_13));
  Adder #(.width(4)) adder_2 (.a(out_13), .b(_0_Q3_Q2_Q1), .out(out_15));  // open: cin, cout

  // Notes on the sheet:
  //   C A3 A2 A1
  //   A0 Q3 Q2 Q1
endmodule
